// Logisim project exam1.circ as structural Verilog: 1 circuit, main circuit vote0
module vote0 (
  input  i1,
  input  i2,
  input  i3,
  input  i4,
  input  i5,
  output o
);

  wire and_1_out, and_2_out, and_3_out, and_4_out, and_5_out, and_6_out, and_7_out, and_8_out, and_9_out,
       and_10_out;

  and and_1 (and_1_out, i3, i4, i5);
  and and_2 (and_2_out, i2, i4, i5);
  and and_3 (and_3_out, i2, i3, i5);
  and and_4 (and_4_out, i2, i3, i4);
  and and_5 (and_5_out, i1, i4, i5);
  and and_6 (and_6_out, i1, i3, i5);
  and and_7 (and_7_out, i1, i3, i4);
  and and_8 (and_8_out, i1, i2, i5);
  and and_9 (and_9_out, i1, i2, i4);
  and and_10 (and_10_out, i1, i2, i3);
  or or_1 (o, and_1_out, and_2_out, and_3_out, and_4_out, and_5_out, and_6_out, and_7_out, and_8_out, and_9_out, and_10_out);
endmodule
