// Logisim project exam3.circ as structural Verilog: 1 circuit, main circuit fence
module fence (
  input  [7:0] plaintext,
  input  [3:0] row,
  output [7:0] ciphertext
);

  wire and_1_out, not_1_out;

  not not_1 (not_1_out, row[1]);
  and and_1 (and_1_out, not_1_out, row[2]);
  Multiplexer #(.width(8)) multiplexer_1 (
    .in0({plaintext[7], plaintext[5], plaintext[3], plaintext[1], plaintext[6], plaintext[4], plaintext[2], plaintext[0]}),
    .in1({plaintext[7], plaintext[3], plaintext[6], plaintext[2], plaintext[5], plaintext[1], plaintext[4], plaintext[0]}),
    .out(ciphertext), .sel(and_1_out));  // open: en
endmodule
