// Logisim project test2.circ as structural Verilog: 1 circuit, main circuit test2
module test2 (
  input  [31:0] in_1,
  input  [31:0] in_2,
  input  [31:0] in_3,
  output [31:0] out_4
);

  wire [31:0] adder_1_out;

  Adder #(.width(32)) adder_1 (.a(in_1), .b(in_2), .out(adder_1_out));  // open: cin, cout
  Subtractor #(.width(32)) subtractor_1 (.a(adder_1_out), .b(in_3), .out(out_4));  // open: bin, bout
endmodule
