// Logisim project test3.circ as structural Verilog: 1 circuit, main circuit test3
module test3 (
  input  [7:0] in_1,
  input  [7:0] in_2,
  input  [7:0] in_3,
  input  [7:0] in_4,
  input  [1:0] in_5,
  output [7:0] out_6
);

  wire [7:0] multiplexer_1_out, multiplexer_2_out;

  Multiplexer #(.width(8)) multiplexer_1 (.in0(in_1), .in1(in_2), .out(multiplexer_1_out), .sel(in_5[0]));  // open: en
  Multiplexer #(.width(8)) multiplexer_2 (.in0(in_3), .in1(in_4), .out(multiplexer_2_out), .sel(in_5[0]));  // open: en
  Multiplexer #(.width(8)) multiplexer_3 (
    .in0(multiplexer_1_out), .in1(multiplexer_2_out), .out(out_6), .sel(in_5[1]));  // open: en
endmodule
