// Logisim project test1.circ as structural Verilog: 1 circuit, main circuit test1
module test1 (
  input  in_1,
  input  in_2,
  input  in_3,
  input  in_4,
  output out_5
);

  wire and_1_out, and_2_out, not_1_out;

  not not_1 (not_1_out, in_1);
  and and_1 (and_1_out, not_1_out, in_2);
  and and_2 (and_2_out, in_1, in_4);
  or or_1 (out_5, and_1_out, and_2_out, in_3);
endmodule
