// Logisim project test3.circ as structural Verilog: 1 circuit, main circuit 2nmod5
module _2nmod5 (
  input  i,
  output [2:0] out_2
);

  wire and_2_out, and_3_out, clock_1_out, not_1_out, not_2_out, not_3_out;
  wire [1:0] d_ff_2_q;

  Clock clock_1 (.out(clock_1_out));
  D_Flip_Flop d_ff_1 (.clk(clock_1_out), .D(d_ff_2_q[0]), .Q(d_ff_2_q[1]));  // open: Qn, preset, en, reset
  D_Flip_Flop d_ff_2 (.clk(clock_1_out), .D(i), .Q(d_ff_2_q[0]));  // open: Qn, preset, en, reset
  // Probe on d_ff_2_q
  not not_1 (not_1_out, i);
  not not_2 (not_2_out, d_ff_2_q[0]);
  not not_3 (not_3_out, i);
  and and_1 (out_2[2], d_ff_2_q[0], not_1_out);
  and and_2 (and_2_out, not_2_out, not_3_out);
  and and_3 (and_3_out, d_ff_2_q[0], i);
  or or_1 (out_2[0], and_2_out, and_3_out);
  // Probe on {out_2[2], i, out_2[0]}

  assign out_2[1] = i;
endmodule
