// Logisim project test4.circ as structural Verilog: 1 circuit, main circuit check
module check (
  input  [8:0] in_1,
  output [7:0] out_2
);

  wire odd_parity_1_out;

  xor odd_parity_1 (odd_parity_1_out, in_1[1], in_1[2], in_1[3], in_1[4], in_1[5], in_1[6], in_1[7], in_1[8], in_1[0]);
  Multiplexer #(.width(8)) multiplexer_1 (
    .in0(in_1[8:1]), .in1({8{1'b1}}), .out(out_2), .sel(odd_parity_1_out));  // open: en
endmodule
