// Logisim project test5.circ as structural Verilog: 1 circuit, main circuit sort
module sort (
  input  [3:0] i1,
  input  [3:0] i2,
  input  [3:0] i3,
  input  [3:0] i4,
  output [3:0] o1,
  output [3:0] o2,
  output [3:0] o3,
  output [3:0] o4
);

  wire comparator_1_gt, comparator_1_lt, comparator_2_gt, comparator_2_lt, comparator_3_gt, comparator_3_lt,
       comparator_4_gt, comparator_4_lt, comparator_5_gt, comparator_5_lt;
  wire [3:0] multiplexer_1_out, multiplexer_2_out, multiplexer_3_out, multiplexer_4_out, multiplexer_6_out,
       multiplexer_7_out;

  Comparator #(.width(4), .mode("unsigned")) comparator_1 (
    .a(i2), .b(i1), .gt(comparator_1_gt), .lt(comparator_1_lt));  // open: eq
  Comparator #(.width(4), .mode("unsigned")) comparator_2 (
    .a(i4), .b(i3), .gt(comparator_2_gt), .lt(comparator_2_lt));  // open: eq
  // Probe on multiplexer_1_out
  Multiplexer #(.width(4)) multiplexer_1 (
    .in0(i1), .in1(i2), .out(multiplexer_1_out), .sel(comparator_1_gt));  // open: en
  // Probe on multiplexer_2_out
  Multiplexer #(.width(4)) multiplexer_2 (
    .in0(i1), .in1(i2), .out(multiplexer_2_out), .sel(comparator_1_lt));  // open: en
  // Probe on multiplexer_3_out
  Multiplexer #(.width(4)) multiplexer_3 (
    .in0(i3), .in1(i4), .out(multiplexer_3_out), .sel(comparator_2_gt));  // open: en
  // Probe on multiplexer_4_out
  Multiplexer #(.width(4)) multiplexer_4 (
    .in0(i3), .in1(i4), .out(multiplexer_4_out), .sel(comparator_2_lt));  // open: en
  Comparator #(.width(4), .mode("unsigned")) comparator_3 (
    .a(multiplexer_1_out), .b(multiplexer_3_out), .gt(comparator_3_gt), .lt(comparator_3_lt));  // open: eq
  Comparator #(.width(4), .mode("unsigned")) comparator_4 (
    .a(multiplexer_2_out), .b(multiplexer_4_out), .gt(comparator_4_gt), .lt(comparator_4_lt));  // open: eq
  Multiplexer #(.width(4)) multiplexer_5 (
    .in0(multiplexer_3_out), .in1(multiplexer_1_out), .out(o1), .sel(comparator_3_gt));  // open: en
  Multiplexer #(.width(4)) multiplexer_6 (
    .in0(multiplexer_3_out), .in1(multiplexer_1_out), .out(multiplexer_6_out), .sel(comparator_3_lt));  // open: en
  Multiplexer #(.width(4)) multiplexer_7 (
    .in0(multiplexer_4_out), .in1(multiplexer_2_out), .out(multiplexer_7_out), .sel(comparator_4_gt));  // open: en
  Multiplexer #(.width(4)) multiplexer_8 (
    .in0(multiplexer_4_out), .in1(multiplexer_2_out), .out(o4), .sel(comparator_4_lt));  // open: en
  // Probe on o1
  // Probe on multiplexer_6_out
  // Probe on multiplexer_7_out
  // Probe on o4
  Comparator #(.width(4), .mode("unsigned")) comparator_5 (
    .a(multiplexer_6_out), .b(multiplexer_7_out), .gt(comparator_5_gt), .lt(comparator_5_lt));  // open: eq
  // Probe on o2
  Multiplexer #(.width(4)) multiplexer_9 (
    .in0(multiplexer_7_out), .in1(multiplexer_6_out), .out(o2), .sel(comparator_5_gt));  // open: en
  // Probe on o3
  Multiplexer #(.width(4)) multiplexer_10 (
    .in0(multiplexer_7_out), .in1(multiplexer_6_out), .out(o3), .sel(comparator_5_lt));  // open: en
endmodule
