// Logisim project cpu_1.circ as structural Verilog: 8 circuits, main circuit main
module main (
  input  in_1,
  output [31:0] out_2,
  output out_3,
  output [4:0] out_4,
  output [31:0] out_5,
  output out_6,
  output [4:0] out_7,
  output [31:0] out_8
);

  wire aludst, alusrc, and_1_out, branch, clk, extop, jump, MemtoReg, zero;
  wire [2:0] aluop;
  wire [4:0] rd, rs, rt, s;
  wire [5:0] Func, Op;
  wire [15:0] imme;
  wire [25:0] instr_index;
  wire [31:0] alu_1_result, ext_1_out_3, ext_2_out_3, grf_1_rd1, multiplexer_2_out, ram_1_data,
       shifter_1_out, shifter_2_out;

  Clock clock_1 (.out(clk));
  Multiplexer #(.width(5), .enable("false")) multiplexer_1 (.in0(rt), .in1(rd), .out(out_4), .sel(aludst));
  grf_2 grf_1 (
    .A1(rs), .A2(rt), .A3(out_4), .WD(out_5), .clk(clk), .reset(in_1), .we(out_3), .RD1(grf_1_rd1),
    .RD2(out_8));
  Multiplexer #(.width(32), .enable("false")) multiplexer_2 (
    .in0(out_8), .in1(ext_1_out_3), .out(multiplexer_2_out), .sel(alusrc));
  ext ext_1 (.in_1(imme), .extop(extop), .out_3(ext_1_out_3));
  Control control_1 (
    .op(Op), .func(Func), .out_3(MemtoReg), .out_4(out_6), .out_5(branch), .out_6(aluop), .out_7(alusrc),
    .out_8(aludst), .out_9(out_3), .out_10(extop), .out_11(jump));
  ext ext_2 (.in_1(imme), .extop(extop), .out_3(ext_2_out_3));
  alu alu_1 (.SrcA(grf_1_rd1), .SrcB(multiplexer_2_out), .s(s), .ALUop(aluop), .zero(zero), .result(alu_1_result));
  and and_1 (and_1_out, zero, branch);
  Shifter #(.width(32)) shifter_1 (.in(ext_2_out_3), .\dist (5'b00010), .out(shifter_1_out));
  Shifter #(.width(32), .shift("lr")) shifter_2 (.in(alu_1_result), .\dist (5'b00010), .out(shifter_2_out));
  ifu ifu_1 (
    .branch(and_1_out), .branchAddr(shifter_1_out), .jump(jump), .jumpAddr(instr_index), .clk(clk),
    .rst(in_1), .OpCode(out_2));
  Bit_Extender #(.in_width(32), .out_width(5)) bit_extender_1 (.in(shifter_2_out), .out(out_7));
  Multiplexer #(.width(32), .enable("false")) multiplexer_3 (
    .in0(alu_1_result), .in1(ram_1_data), .out(out_5), .sel(MemtoReg));
  RAM #(.addrWidth(5), .dataWidth(32), .bus("separate")) ram_1 (
    .addr(out_7), .din(out_8), .data(ram_1_data), .str(out_6), .clk(clk), .clr(in_1));  // open: sel, ld
  Spliter spliter_1 (
    .insturcture(out_2), .Op(Op), .Func(Func), .rs(rs), .rt(rt), .rd(rd), .s(s), .imme(imme),
    .instr_index(instr_index));

  // Other names for the same wires on the sheet: ins[31:0] = out_2; MemAddr[4:0] = out_7; MemData[31:0] = out_8;
  //   MemWrite = out_6; RegAddr[4:0] = out_4; RegData[31:0] = out_5; RegWrite = out_3; rst = in_1
endmodule

// ALU
module alu (
  input  [31:0] SrcA,
  input  [31:0] SrcB,
  input  [4:0] s,
  input  [2:0] ALUop,
  output zero,
  output [31:0] result
);

  wire [31:0] adder_1_out, and_1_out, or_1_out, shifter_1_out, shifter_2_out, subtractor_1_out;

  assign and_1_out = SrcA & SrcB;  // AND_Gate and_1, 32 bits wide
  assign or_1_out = SrcA | SrcB;  // OR_Gate or_1, 32 bits wide
  Adder #(.width(32)) adder_1 (.a(SrcA), .b(SrcB), .out(adder_1_out));  // open: cin, cout
  Shifter #(.width(32)) shifter_1 (.in(SrcB), .\dist (s), .out(shifter_1_out));
  Subtractor #(.width(32)) subtractor_1 (.a(SrcA), .b(SrcB), .out(subtractor_1_out));  // open: bin, bout
  Shifter #(.width(32)) shifter_2 (.in(SrcB), .\dist (5'b10000), .out(shifter_2_out));
  Multiplexer #(.select(3), .width(32), .enable("false")) multiplexer_1 (
    .in0(and_1_out), .in1(or_1_out), .in2(adder_1_out), .in3(shifter_1_out), .in6(subtractor_1_out),
    .in7(shifter_2_out), .out(result), .sel(ALUop));  // open: in4, in5
  Comparator #(.width(32), .mode("unsigned")) comparator_1 (.a({32{1'b0}}), .b(result), .eq(zero));  // open: gt, lt
endmodule

// IFU
module ifu (
  input  branch,
  input  [31:0] branchAddr,
  input  jump,
  input  clk,
  input  rst,
  input  [25:0] jumpAddr,
  output [31:0] OpCode
);

  wire [4:0] bit_extender_2_out;
  wire [31:0] adder_1_out, adder_2_out, adder_3_out, and_1_out, bit_extender_1_out, multiplexer_1_out,
       multiplexer_2_out, or_1_out, PC_q, shifter_1_out, shifter_2_out;

  assign and_1_out = PC_q & 32'hf0000000;  // AND_Gate and_1, 32 bits wide
  assign bit_extender_1_out = {{6{1'b0}}, jumpAddr};  // Bit_Extender bit_extender_1
  Shifter #(.width(32)) shifter_1 (.in(bit_extender_1_out), .\dist (5'b00010), .out(shifter_1_out));
  Adder #(.width(32)) adder_1 (.a(adder_2_out), .b(branchAddr), .out(adder_1_out));  // open: cin, cout
  assign or_1_out = and_1_out | shifter_1_out;  // OR_Gate or_1, 32 bits wide
  Multiplexer #(.width(32), .enable("false")) multiplexer_1 (
    .in0(adder_2_out), .in1(adder_1_out), .out(multiplexer_1_out), .sel(branch));
  Register #(.width(32)) PC (.D(multiplexer_2_out), .Q(PC_q), .clk(clk), .clr(rst));  // open: en
  Multiplexer #(.width(32), .enable("false")) multiplexer_2 (
    .in0(multiplexer_1_out), .in1(or_1_out), .out(multiplexer_2_out), .sel(jump));
  Adder #(.width(32)) adder_2 (.a(32'h4), .b(PC_q), .out(adder_2_out));  // open: cin, cout
  Adder #(.width(32)) adder_3 (.a(PC_q), .b(32'h3000), .out(adder_3_out));  // open: cin, cout
  Bit_Extender #(.in_width(32), .out_width(5)) bit_extender_2 (.in(shifter_2_out), .out(bit_extender_2_out));
  Shifter #(.width(32), .shift("lr")) shifter_2 (.in(adder_3_out), .\dist (5'b00010), .out(shifter_2_out));
  ROM #(.addrWidth(5), .dataWidth(32)) rom_1 (.addr(bit_extender_2_out), .data(OpCode));  // open: sel
endmodule

module Control (
  input  [5:0] op,
  input  [5:0] func,
  output out_3,
  output out_4,
  output out_5,
  output [2:0] out_6,
  output out_7,
  output out_8,
  output out_9,
  output out_10,
  output out_11
);

  wire addu, beq, j, lui, lw, ori, sll, subu, sw;

  and and_1 (addu, ~op[0], ~op[1], ~op[2], ~op[3], ~op[4], ~op[5], func[0], ~func[1], ~func[2], ~func[3], ~func[4], func[5]);  // AND_Gate
  and and_2 (ori, op[0], ~op[1], op[2], op[3], ~op[4], ~op[5]);  // AND_Gate
  and and_3 (sw, op[0], op[1], ~op[2], op[3], ~op[4], op[5]);  // AND_Gate
  and and_4 (lui, op[0], op[1], op[2], op[3], ~op[4], ~op[5]);  // AND_Gate
  and and_5 (j, ~op[0], op[1], ~op[2], ~op[3], ~op[4], ~op[5]);  // AND_Gate
  and and_6 (subu, ~op[0], ~op[1], ~op[2], ~op[3], ~op[4], ~op[5], func[0], func[1], ~func[2], ~func[3], ~func[4], func[5]);  // AND_Gate
  and and_7 (lw, op[0], op[1], ~op[2], ~op[3], ~op[4], op[5]);  // AND_Gate
  and and_8 (beq, ~op[0], ~op[1], op[2], ~op[3], ~op[4], ~op[5]);  // AND_Gate
  and and_9 (sll, ~op[0], ~op[1], ~op[2], ~op[3], ~op[4], ~op[5], ~func[0], ~func[1], ~func[2], ~func[3], ~func[4], ~func[5]);  // AND_Gate
  or or_1 (out_9, lw, addu, ori, subu, lui, sll);
  or or_2 (out_8, addu, subu, sll);
  or or_3 (out_7, lw, sw, ori, lui);
  buf or_4 (out_5, beq);  // OR_Gate
  buf or_5 (out_10, ori);  // OR_Gate
  buf or_6 (out_11, j);  // OR_Gate
  buf or_7 (out_4, sw);  // OR_Gate
  buf or_8 (out_3, lw);  // OR_Gate
  or or_9 (out_6[2], subu, beq, lui);
  or or_10 (out_6[1], subu, lw, sw, addu, beq, lui, sll);
  or or_11 (out_6[0], ori, lui, sll);

  // Other names for the same wires on the sheet: ALUSrc = out_7; Branch = out_5; ExtOp = out_10; jump = out_11;
  //   MemtoReg = out_3; MemWrite = out_4; ALUOp0 = out_6[0]; ALUOp1 = out_6[1]; ALUOp2 = out_6[2]; RegDst = out_8;
  //   RegWrite = out_9
endmodule

module Spliter (
  input  [31:0] insturcture,
  output [5:0] Op,
  output [5:0] Func,
  output [4:0] rs,
  output [4:0] rt,
  output [4:0] rd,
  output [4:0] s,
  output [15:0] imme,
  output [25:0] instr_index
);


  assign Func = insturcture[5:0];
  assign imme = insturcture[15:0];
  assign instr_index = insturcture[25:0];
  assign Op = insturcture[31:26];
  assign rd = insturcture[15:11];
  assign rs = insturcture[25:21];
  assign rt = insturcture[20:16];
  assign s = insturcture[10:6];
endmodule

// EXT
module ext (
  input  [15:0] in_1,
  input  extop,
  output [31:0] out_3
);

  wire [31:0] bit_extender_1_out, bit_extender_2_out;

  assign bit_extender_1_out = {{16{in_1[15]}}, in_1};  // Bit_Extender bit_extender_1
  assign bit_extender_2_out = {{16{1'b0}}, in_1};  // Bit_Extender bit_extender_2
  Multiplexer #(.width(32), .enable("false")) multiplexer_1 (
    .in0(bit_extender_1_out), .in1(bit_extender_2_out), .out(out_3), .sel(extop));
endmodule

module grf (
  input  in_1,
  input  [4:0] A1,
  input  [4:0] A2,
  input  [4:0] A3,
  input  [31:0] WD,
  input  clk,
  input  rst,
  output [31:0] out_8,
  output [31:0] out_9
);

  wire I0, I1, I2, I3, I4, I5, I6, I7, I8, I9, I10, I11, I12, I13, I14, I15, I16, I17, I18, I19, I20, I21,
       I22, I23, I24, I25, I26, I27, I28, I29, I30, I31;
  wire [31:0] O1, O2, O3, O4, O5, O6, O7, O8, O9, O10, O11, O12, O13, O14, O15, O16, O17, O18, O19, O20, O21,
       O22, O23, O24, O25, O26, O27, O28, O29, O30, O31;

  Register #(.width(32)) register_1 (.D(WD), .en(I0), .clk(clk), .clr(rst));  // open: Q
  Register #(.width(32)) register_2 (.D(WD), .en(I4), .Q(O4), .clk(clk), .clr(rst));
  Register #(.width(32)) register_3 (.D(WD), .en(I8), .Q(O8), .clk(clk), .clr(rst));
  Register #(.width(32)) register_4 (.D(WD), .en(I12), .Q(O12), .clk(clk), .clr(rst));
  Register #(.width(32)) register_5 (.D(WD), .en(I16), .Q(O16), .clk(clk), .clr(rst));
  Register #(.width(32)) register_6 (.D(WD), .en(I20), .Q(O20), .clk(clk), .clr(rst));
  Register #(.width(32)) register_7 (.D(WD), .en(I24), .Q(O24), .clk(clk), .clr(rst));
  Register #(.width(32)) register_8 (.D(WD), .en(I28), .Q(O28), .clk(clk), .clr(rst));
  Register #(.width(32)) register_9 (.D(WD), .en(I1), .Q(O1), .clk(clk), .clr(rst));
  Register #(.width(32)) register_10 (.D(WD), .en(I5), .Q(O5), .clk(clk), .clr(rst));
  Register #(.width(32)) register_11 (.D(WD), .en(I9), .Q(O9), .clk(clk), .clr(rst));
  Register #(.width(32)) register_12 (.D(WD), .en(I13), .Q(O13), .clk(clk), .clr(rst));
  Register #(.width(32)) register_13 (.D(WD), .en(I17), .Q(O17), .clk(clk), .clr(rst));
  Register #(.width(32)) register_14 (.D(WD), .en(I21), .Q(O21), .clk(clk), .clr(rst));
  Register #(.width(32)) register_15 (.D(WD), .en(I25), .Q(O25), .clk(clk), .clr(rst));
  Register #(.width(32)) register_16 (.D(WD), .en(I29), .Q(O29), .clk(clk), .clr(rst));
  Register #(.width(32)) register_17 (.D(WD), .en(I2), .Q(O2), .clk(clk), .clr(rst));
  Register #(.width(32)) register_18 (.D(WD), .en(I6), .Q(O6), .clk(clk), .clr(rst));
  Register #(.width(32)) register_19 (.D(WD), .en(I10), .Q(O10), .clk(clk), .clr(rst));
  Register #(.width(32)) register_20 (.D(WD), .en(I14), .Q(O14), .clk(clk), .clr(rst));
  Register #(.width(32)) register_21 (.D(WD), .en(I18), .Q(O18), .clk(clk), .clr(rst));
  Register #(.width(32)) register_22 (.D(WD), .en(I22), .Q(O22), .clk(clk), .clr(rst));
  Register #(.width(32)) register_23 (.D(WD), .en(I26), .Q(O26), .clk(clk), .clr(rst));
  Register #(.width(32)) register_24 (.D(WD), .en(I30), .Q(O30), .clk(clk), .clr(rst));
  Register #(.width(32)) register_25 (.D(WD), .en(I3), .Q(O3), .clk(clk), .clr(rst));
  Register #(.width(32)) register_26 (.D(WD), .en(I7), .Q(O7), .clk(clk), .clr(rst));
  Register #(.width(32)) register_27 (.D(WD), .en(I11), .Q(O11), .clk(clk), .clr(rst));
  Register #(.width(32)) register_28 (.D(WD), .en(I15), .Q(O15), .clk(clk), .clr(rst));
  Register #(.width(32)) register_29 (.D(WD), .en(I19), .Q(O19), .clk(clk), .clr(rst));
  Register #(.width(32)) register_30 (.D(WD), .en(I23), .Q(O23), .clk(clk), .clr(rst));
  Register #(.width(32)) register_31 (.D(WD), .en(I27), .Q(O27), .clk(clk), .clr(rst));
  Register #(.width(32)) register_32 (.D(WD), .en(I31), .Q(O31), .clk(clk), .clr(rst));
  Decoder #(.select(5)) decoder_1 (
    .out0(I0), .out1(I1), .out2(I2), .out3(I3), .out4(I4), .out5(I5), .out6(I6), .out7(I7), .out8(I8),
    .out9(I9), .out10(I10), .out11(I11), .out12(I12), .out13(I13), .out14(I14), .out15(I15), .out16(I16),
    .out17(I17), .sel(A3), .en(in_1));  // open: out18, out19, out20, out21, out22, out23, out24, out25, out26, out27, out28, out29, out30, out31

  // Other names for the same wires on the sheet: RD1[31:0] = out_8; RD2[31:0] = out_9; WE = in_1
endmodule

// GRF
module grf_2 (
  input  [4:0] A1,
  input  clk,
  input  reset,
  input  we,
  input  [4:0] A2,
  input  [4:0] A3,
  input  [31:0] WD,
  output [31:0] RD1,
  output [31:0] RD2
);

  wire [31:0] I0, I1, I2, I3, I4, I5, I6, I7, I8, I9, I10, I11, I12, I13, I14, I15, I16, I17, I18, I19, I20,
       I21, I22, I23, I24, I25, I26, I27, I28, I29, I30, I31, O0, O1, O2, O3, O4, O5, O6, O7, O8, O9, O10,
       O11, O12, O13, O14, O15, O16, O17, O18, O19, O20, O21, O22, O23, O24, O25, O26, O27, O28, O29, O30,
       O31;

  Demultiplexer #(.select(5), .width(32), .tristate("true")) demultiplexer_1 (
    .out0(I0), .out1(I1), .out2(I2), .out3(I3), .out4(I4), .out5(I5), .out6(I6), .out7(I7), .out8(I8),
    .out9(I9), .out10(I10), .out11(I11), .out12(I12), .out13(I13), .out14(I14), .out15(I15), .out16(I16),
    .out17(I17), .out18(I18), .out19(I19), .out20(I20), .out21(I21), .out22(I22), .out23(I23), .out24(I24),
    .out25(I25), .out26(I26), .out27(I27), .out28(I28), .out29(I29), .out30(I30), .out31(I31), .in(WD),
    .sel(A3));  // open: en
  Multiplexer #(.select(5), .width(32)) multiplexer_1 (
    .in0(O0), .in1(O1), .in2(O2), .in3(O3), .in4(O4), .in5(O5), .in6(O6), .in7(O7), .in8(O8), .in9(O9),
    .in10(O10), .in11(O11), .in12(O12), .in13(O13), .in14(O14), .in15(O15), .in16(O16), .in17(O17),
    .in18(O18), .in19(O19), .in20(O20), .in21(O21), .in22(O22), .in23(O23), .in24(O24), .in25(O25),
    .in26(O26), .in27(O27), .in28(O28), .in29(O29), .in30(O30), .in31(O31), .out(RD2), .sel(A2));  // open: en
  Multiplexer #(.select(5), .width(32)) multiplexer_2 (
    .in0(O0), .in1(O1), .in2(O2), .in3(O3), .in4(O4), .in5(O5), .in6(O6), .in7(O7), .in8(O8), .in9(O9),
    .in10(O10), .in11(O11), .in12(O12), .in13(O13), .in14(O14), .in15(O15), .in16(O16), .in17(O17),
    .in18(O18), .in19(O19), .in20(O20), .in21(O21), .in22(O22), .in23(O23), .in24(O24), .in25(O25),
    .in26(O26), .in27(O27), .in28(O28), .in29(O29), .in30(O30), .in31(O31), .out(RD1), .sel(A1));  // open: en
  Register #(.width(32)) register_1 (.D({32{1'b0}}), .en(we), .Q(O0), .clk(clk), .clr(reset));
  Register #(.width(32)) register_2 (.D(I8), .en(we), .Q(O8), .clk(clk), .clr(reset));
  Register #(.width(32)) register_3 (.D(I16), .en(we), .Q(O16), .clk(clk), .clr(reset));
  Register #(.width(32)) register_4 (.D(I24), .en(we), .Q(O24), .clk(clk), .clr(reset));
  Register #(.width(32)) register_5 (.D(I1), .en(we), .Q(O1), .clk(clk), .clr(reset));
  Register #(.width(32)) register_6 (.D(I9), .en(we), .Q(O9), .clk(clk), .clr(reset));
  Register #(.width(32)) register_7 (.D(I17), .en(we), .Q(O17), .clk(clk), .clr(reset));
  Register #(.width(32)) register_8 (.D(I25), .en(we), .Q(O25), .clk(clk), .clr(reset));
  Register #(.width(32)) register_9 (.D(I2), .en(we), .Q(O2), .clk(clk), .clr(reset));
  Register #(.width(32)) register_10 (.D(I10), .en(we), .Q(O10), .clk(clk), .clr(reset));
  Register #(.width(32)) register_11 (.D(I18), .en(we), .Q(O18), .clk(clk), .clr(reset));
  Register #(.width(32)) register_12 (.D(I26), .en(we), .Q(O26), .clk(clk), .clr(reset));
  Register #(.width(32)) register_13 (.D(I3), .en(we), .Q(O3), .clk(clk), .clr(reset));
  Register #(.width(32)) register_14 (.D(I11), .en(we), .Q(O11), .clk(clk), .clr(reset));
  Register #(.width(32)) register_15 (.D(I19), .en(we), .Q(O19), .clk(clk), .clr(reset));
  Register #(.width(32)) register_16 (.D(I27), .en(we), .Q(O27), .clk(clk), .clr(reset));
  Register #(.width(32)) register_17 (.D(I4), .en(we), .Q(O4), .clk(clk), .clr(reset));
  Register #(.width(32)) register_18 (.D(I12), .en(we), .Q(O12), .clk(clk), .clr(reset));
  Register #(.width(32)) register_19 (.D(I20), .en(we), .Q(O20), .clk(clk), .clr(reset));
  Register #(.width(32)) register_20 (.D(I28), .en(we), .Q(O28), .clk(clk), .clr(reset));
  Register #(.width(32)) register_21 (.D(I5), .en(we), .Q(O5), .clk(clk), .clr(reset));
  Register #(.width(32)) register_22 (.D(I13), .en(we), .Q(O13), .clk(clk), .clr(reset));
  Register #(.width(32)) register_23 (.D(I21), .en(we), .Q(O21), .clk(clk), .clr(reset));
  Register #(.width(32)) register_24 (.D(I29), .en(we), .Q(O29), .clk(clk), .clr(reset));
  Register #(.width(32)) register_25 (.D(I6), .en(we), .Q(O6), .clk(clk), .clr(reset));
  Register #(.width(32)) register_26 (.D(I14), .en(we), .Q(O14), .clk(clk), .clr(reset));
  Register #(.width(32)) register_27 (.D(I22), .en(we), .Q(O22), .clk(clk), .clr(reset));
  Register #(.width(32)) register_28 (.D(I30), .en(we), .Q(O30), .clk(clk), .clr(reset));
  Register #(.width(32)) register_29 (.D(I7), .en(we), .Q(O7), .clk(clk), .clr(reset));
  Register #(.width(32)) register_30 (.D(I15), .en(we), .Q(O15), .clk(clk), .clr(reset));
  Register #(.width(32)) register_31 (.D(I23), .en(we), .Q(O23), .clk(clk), .clr(reset));
  Register #(.width(32)) register_32 (.D(I31), .en(we), .Q(O31), .clk(clk), .clr(reset));
endmodule
