// Logisim project p4.circ as structural Verilog: 14 circuits, main circuit main
module main (
  input  in_1,
  output [31:0] Instr,
  output RegWrite,
  output [4:0] RegAddr,
  output [31:0] RegData,
  output MemWrite,
  output [4:0] MemAddr,
  output [31:0] MemData
);

  wire beq, clk, EX_AluSrc, EX_MemRead, EX_MemWrite, EX_RegWrite, flushE, fRtMsel, ID_AluSrc, ID_equ,
       ID_MemRead, ID_MemWrite, ID_RegWrite, ID_s1, ID_s2, jr, jump, MEM_MemRead, MEM_MemWrite, MEM_RegWrite,
       stallD, stallF;
  wire [1:0] dereg_1_rs_o, EX_MemtoReg, extop, fRsDsel, fRsEsel, fRtDsel, fRtEsel, ID_MemtoReg, ID_RegDst,
       ID_tuse1, ID_tuse2, MEM_MemtoReg, mwreg_1_out_18;
  wire [2:0] dereg_1_rs_o_7, ID_AluOp;
  wire [3:0] EX_tnew, ID_tnew, MEM_tnew, WB_tnew;
  wire [4:0] dereg_1_rd_o, dereg_1_rt_o, des_E, des_M, des_W, EX_WriteRegDst, MEM_WriteRegDst, rd, rs, rt, s,
       s1_D, s1_E, s2_D, s2_E, s2_M;
  wire [5:0] spliter_1_func, spliter_1_op;
  wire [9:0] ifu_1_instr_o;
  wire [15:0] imme16;
  wire [25:0] imme26;
  wire [31:0] alu_1_result, dereg_1_extres_2, dereg_1_rd1_o, dereg_1_rd2_o, emreg_1_out_20, emreg_1_out_21,
       EX_instr, EX_pc, EX_pc4, EX_pc8, EX_WriteData, extres, fEX, fMEM, grf_1_rd1, grf_1_rd2, ID_instr,
       ID_pc, ID_pc4, ID_pc8, ifu_1_pc_o, MEM_instr, MEM_pc, MEM_pc4, MEM_pc8, MemAddr_t, multiplexer_6_out,
       multiplexer_7_out, multiplexer_9_out, multiplexer_11_out, multiplexer_13_out, mwreg_1_out_19,
       mwreg_1_out_21, mwreg_1_pc_8_o, npc, ram_1_data, undriven, WB_instr;

  Clock clock_1 (.out(clk));
  // Probe on ID_instr
  // Probe on EX_instr
  // Probe on MEM_instr
  // Probe on WB_instr
  IFU ifu_1 (.pc_i(npc), .instr_o(ifu_1_instr_o), .pc_o(ifu_1_pc_o), .in_1(clk), .in_2(in_1), .in_4(stallF));
  // Probe on ifu_1_pc_o
  ROM #(.addrWidth(10), .dataWidth(32)) rom_1 (.addr(ifu_1_instr_o), .data(Instr));  // open: sel
  NPC npc_1 (
    .pc(ifu_1_pc_o), .branchaddr(extres), .imme26(imme26), .reg31(undriven), .npc(npc), .beq(beq),
    .jump(jump), .jr(jr), .equ(ID_equ));
  forwardUnit forwardunit_1 (
    .s1_D(s1_D), .s2_D(s2_D), .s1_E(s1_E), .s2_E(s2_E), .des_E(des_E), .tNew_E(EX_tnew), .s2_M(s2_M),
    .tNew_M(MEM_tnew), .des_M(des_M), .tNew_W(WB_tnew), .des_W(des_W), .fRsDsel(fRsDsel), .fRtDsel(fRtDsel),
    .fRsEsel(fRsEsel), .fRtEsel(fRtEsel), .fRtMsel(fRtMsel));
  FDreg fdreg_1 (
    .instr_i(Instr), .pc_i(ifu_1_pc_o), .instr_o(ID_instr), .pc_o(ID_pc), .in_1(clk), .in_2(in_1),
    .in_5(stallD), .pc_o_2(ID_pc4), .pc_o_3(ID_pc8));
  Multiplexer #(.width(5), .enable("false")) multiplexer_1 (.in0({5{1'b0}}), .in1(rs), .out(s1_D), .sel(ID_s1));
  Multiplexer #(.width(5), .enable("false")) multiplexer_2 (.in0({5{1'b0}}), .in1(rt), .out(s2_D), .sel(ID_s2));
  Spliter spliter_1 (
    .insturcture(ID_instr), .Op(spliter_1_op), .Func(spliter_1_func), .instr_index(imme26), .imme(imme16),
    .rs(rs), .rt(rt), .rd(rd), .s(s));
  Multiplexer #(.width(5), .enable("false")) multiplexer_3 (
    .in0({5{1'b0}}), .in1(EX_WriteRegDst), .out(des_E), .sel(EX_RegWrite));
  Multiplexer #(.width(5), .enable("false")) multiplexer_4 (
    .in0({5{1'b0}}), .in1(MEM_WriteRegDst), .out(des_M), .sel(MEM_RegWrite));
  Multiplexer #(.width(5), .enable("false")) multiplexer_5 (
    .in0({5{1'b0}}), .in1(RegAddr), .out(des_W), .sel(RegWrite));
  Control control_1 (
    .op(spliter_1_op), .func(spliter_1_func), .out_10(ID_s1), .out_12(ID_s2), .out_3(ID_MemtoReg),
    .out_4(ID_MemRead), .out_5(ID_MemWrite), .out_6(beq), .out_7(ID_AluOp), .out_8(ID_AluSrc),
    .out_9(ID_RegDst), .out_11(ID_RegWrite), .out_13(extop), .out_16(jump), .out_14(ID_tuse1),
    .out_15(ID_tuse2), .out_17(ID_tnew));
  grf grf_1 (
    .A1(rs), .A2(rt), .A3(RegAddr), .WD(RegData), .RD1(grf_1_rd1), .RD2(grf_1_rd2), .clk(clk), .reset(in_1),
    .we(RegWrite));
  stall stall_1 (
    .s1_D(s1_D), .s2_D(s2_D), .tUse1_D(ID_tuse1), .tUse2_D(ID_tuse2), .des_E(des_E), .tNew_E(EX_tnew),
    .tNew_M(MEM_tnew), .des_M(des_M), .Stall_F(stallF), .Stall_D(stallD), .flush_E(flushE));
  // Probe on multiplexer_6_out
  Multiplexer #(.select(2), .width(32), .enable("false")) multiplexer_6 (
    .in0(grf_1_rd1), .in1(fEX), .in2(fMEM), .out(multiplexer_6_out), .sel(fRsDsel));  // open: in3
  Multiplexer #(.select(2), .width(32), .enable("false")) multiplexer_7 (
    .in0(grf_1_rd2), .in1(fEX), .in2(fMEM), .out(multiplexer_7_out), .sel(fRtDsel));  // open: in3
  ext ext_1 (.in_1(imme16), .extop(extop), .out_3(extres));
  // Probe on multiplexer_7_out
  Comparator #(.width(32), .mode("unsigned")) comparator_1 (
    .a(multiplexer_7_out), .b(multiplexer_6_out), .eq(ID_equ));  // open: gt, lt
  DEreg dereg_1 (
    .regdst(ID_RegDst), .regwrite(ID_RegWrite), .alusrc(ID_AluSrc), .memread(ID_MemRead),
    .memwrite(ID_MemWrite), .memtoreg(ID_MemtoReg), .aluop(ID_AluOp), .RD1_i(multiplexer_6_out),
    .RD2_i(multiplexer_7_out), .rs_i(rs), .rt_i(rt), .rd_i(rd), .pc_i(ID_pc), .pc_4_i(ID_pc4),
    .pc_8_i(ID_pc8), .extres(extres), .instr_i(ID_instr), .s1(s1_D), .s1_2(s2_D), .rs_o(dereg_1_rs_o),
    .rs_o_2(EX_RegWrite), .rs_o_3(EX_AluSrc), .rs_o_4(EX_MemRead), .rs_o_5(EX_MemWrite),
    .rs_o_6(EX_MemtoReg), .rs_o_7(dereg_1_rs_o_7), .RD1_o(dereg_1_rd1_o), .RD2_o(dereg_1_rd2_o),
    .rt_o(dereg_1_rt_o), .rd_o(dereg_1_rd_o), .pc_o(EX_pc), .pc_4_o(EX_pc4), .pc_8_o(EX_pc8),
    .extres_2(dereg_1_extres_2), .out_40(EX_instr), .tnew_2(EX_tnew), .s1_3(s1_E), .s1_4(s2_E), .in_1(clk),
    .in_2(in_1), .in_13(flushE), .tnew(ID_tnew));  // open: rs_o_8
  Multiplexer #(.select(2), .width(5), .enable("false")) multiplexer_8 (
    .in0(dereg_1_rt_o), .in1(dereg_1_rd_o), .in2({5{1'b1}}), .out(EX_WriteRegDst), .sel(dereg_1_rs_o));  // open: in3
  Multiplexer #(.select(2), .width(32), .enable("false")) multiplexer_9 (
    .in0(dereg_1_rd1_o), .in1(fMEM), .in2(RegData), .out(multiplexer_9_out), .sel(fRsEsel));  // open: in3
  Multiplexer #(.select(2), .width(32), .enable("false")) multiplexer_10 (
    .in0(dereg_1_rd2_o), .in1(fMEM), .in2(RegData), .out(EX_WriteData), .sel(fRtEsel));  // open: in3
  Multiplexer #(.width(32), .enable("false")) multiplexer_11 (
    .in0(EX_WriteData), .in1(dereg_1_extres_2), .out(multiplexer_11_out), .sel(EX_AluSrc));
  alu alu_1 (
    .SrcA(multiplexer_9_out), .SrcB(multiplexer_11_out), .result(alu_1_result), .ALUop(dereg_1_rs_o_7));  // open: s, zero
  Multiplexer #(.select(2), .width(32), .enable("false")) multiplexer_12 (
    .in0(dereg_1_extres_2), .in2(EX_pc8), .out(fEX), .sel(EX_MemtoReg));  // open: in1, in3
  EMreg emreg_1 (
    .memwrite(EX_MemWrite), .regwrite(EX_RegWrite), .memread(EX_MemRead), .memtoreg(EX_MemtoReg),
    .aluresult_i(alu_1_result), .writedata_i(EX_WriteData), .writereg_i(EX_WriteRegDst), .pc_i(EX_pc),
    .pc_4_i(EX_pc4), .pc_8_i(EX_pc8), .instr_i(EX_instr), .tnew(EX_tnew), .s2(s2_E), .out_16(MEM_MemWrite),
    .out_17(MEM_RegWrite), .out_18(MEM_MemRead), .out_19(MEM_MemtoReg), .out_20(emreg_1_out_20),
    .out_21(emreg_1_out_21), .out_22(MEM_WriteRegDst), .pc_o(MEM_pc), .pc_4_o(MEM_pc4), .pc_8_o(MEM_pc8),
    .out_26(MEM_instr), .out_27(MEM_tnew), .out_28(s2_M), .in_1(clk), .in_2(in_1));
  Multiplexer #(.width(32), .enable("false")) multiplexer_13 (
    .in0(emreg_1_out_21), .in1(RegData), .out(multiplexer_13_out), .sel(fRtMsel));
  RAM #(.addrWidth(5), .dataWidth(32), .bus("separate")) ram_1 (
    .addr(emreg_1_out_20[6:2]), .din(multiplexer_13_out), .data(ram_1_data), .str(MEM_MemWrite), .clk(clk),
    .clr(in_1));  // open: sel, ld
  Multiplexer #(.select(2), .width(32), .enable("false")) multiplexer_14 (
    .in0(emreg_1_out_20), .in1(ram_1_data), .in2(MEM_pc8), .out(fMEM), .sel(MEM_MemtoReg));  // open: in3
  MWreg mwreg_1 (
    .memwrite(MEM_RegWrite), .memwrite_2(MEM_MemtoReg), .aluresult_i(emreg_1_out_20),
    .writedata_i(emreg_1_out_21), .readdata_i(ram_1_data), .pc_i(MEM_pc), .pc_4_i(MEM_pc4), .pc_8_i(MEM_pc8),
    .instr_i(MEM_instr), .writereg_i(MEM_WriteRegDst), .memaddr(emreg_1_out_20),
    .memdata(multiplexer_13_out), .memwrite_3(MEM_MemWrite), .tnew(MEM_tnew), .out_17(RegWrite),
    .out_18(mwreg_1_out_18), .out_19(mwreg_1_out_19), .out_21(mwreg_1_out_21), .pc_8_o(mwreg_1_pc_8_o),
    .out_25(WB_instr), .out_26(RegAddr), .out_27({MemAddr_t[31:7], MemAddr, MemAddr_t[1:0]}),
    .out_28(MemData), .out_29(MemWrite), .out_30(WB_tnew), .in_1(clk), .in_2(in_1));  // open: out_20, pc_o, pc_4_o
  Multiplexer #(.select(2), .width(32), .enable("false")) multiplexer_15 (
    .in0(mwreg_1_out_19), .in1(mwreg_1_out_21), .in2(mwreg_1_pc_8_o), .out(RegData), .sel(mwreg_1_out_18));  // open: in3

  // Other names for the same wires on the sheet: fWB[31:0] = RegData; WB_RegData[31:0] = RegData;
  //   MemAddr_t[6:2] = MemAddr; rst = in_1; WB_RegWrite = RegWrite; WB_WriteRegDst[4:0] = RegAddr

  // Notes on the sheet:
  //   contents of rom_1 (hex, n*v repeats v):
  //   36100000 36310003 36f70003 ae110000 8e120000 12f20001 36530004 ae130004
endmodule

// ALU
module alu (
  input  [31:0] SrcA,
  input  [31:0] SrcB,
  input  [4:0] s,
  input  [2:0] ALUop,
  output [31:0] result,
  output zero
);

  wire [31:0] adder_1_out, and_1_out, or_1_out, shifter_1_out, shifter_2_out, subtractor_1_out;

  assign and_1_out = SrcA & SrcB;  // AND_Gate and_1, 32 bits wide
  assign or_1_out = SrcA | SrcB;  // OR_Gate or_1, 32 bits wide
  Adder #(.width(32)) adder_1 (.a(SrcA), .b(SrcB), .out(adder_1_out));  // open: cin, cout
  Shifter #(.width(32)) shifter_1 (.in(SrcB), .\dist (s), .out(shifter_1_out));
  Subtractor #(.width(32)) subtractor_1 (.a(SrcA), .b(SrcB), .out(subtractor_1_out));  // open: bin, bout
  Shifter #(.width(32)) shifter_2 (.in(SrcB), .\dist (5'b10000), .out(shifter_2_out));
  Multiplexer #(.select(3), .width(32), .enable("false")) multiplexer_1 (
    .in0(and_1_out), .in1(or_1_out), .in2(adder_1_out), .in3(shifter_1_out), .in6(subtractor_1_out),
    .in7(shifter_2_out), .out(result), .sel(ALUop));  // open: in4, in5
  Comparator #(.width(32), .mode("unsigned")) comparator_1 (.a({32{1'b0}}), .b(result), .eq(zero));  // open: gt, lt
endmodule

module Control (
  input  [5:0] op,
  input  [5:0] func,
  output [1:0] out_3,
  output out_4,
  output out_5,
  output out_6,
  output [2:0] out_7,
  output out_8,
  output [1:0] out_9,
  output out_10,
  output out_11,
  output out_12,
  output [1:0] out_13,
  output [1:0] out_14,
  output [1:0] out_15,
  output out_16,
  output [3:0] out_17
);

  wire addu, beq, j, jal, lui, lw, or_11_out, or_12_out, or_13_out, or_20_out, ori, subu, sw;
  wire [1:0] multiplexer_2_out;
  wire [3:0] multiplexer_1_out, multiplexer_5_out;

  and and_1 (addu, ~op[0], ~op[1], ~op[2], ~op[3], ~op[4], ~op[5], func[0], ~func[1], ~func[2], ~func[3], ~func[4], func[5]);  // AND_Gate
  and and_2 (ori, op[0], ~op[1], op[2], op[3], ~op[4], ~op[5]);  // AND_Gate
  and and_3 (sw, op[0], op[1], ~op[2], op[3], ~op[4], op[5]);  // AND_Gate
  and and_4 (lui, op[0], op[1], op[2], op[3], ~op[4], ~op[5]);  // AND_Gate
  and and_5 (j, ~op[0], op[1], ~op[2], ~op[3], ~op[4], ~op[5]);  // AND_Gate
  and and_6 (jal, op[0], op[1], ~op[2], ~op[3], ~op[4], ~op[5]);  // AND_Gate
  and and_7 (subu, ~op[0], ~op[1], ~op[2], ~op[3], ~op[4], ~op[5], func[0], func[1], ~func[2], ~func[3], ~func[4], func[5]);  // AND_Gate
  and and_8 (lw, op[0], op[1], ~op[2], ~op[3], ~op[4], op[5]);  // AND_Gate
  and and_9 (beq, ~op[0], ~op[1], op[2], ~op[3], ~op[4], ~op[5]);  // AND_Gate
  // AND_Gate and_10 has open pins: in0=op[0], in1=op[1], in2=op[2], in3=op[3], in4=op[4], in5=op[5], in6=func[0], in7=func[1], in8=func[2], in9=func[3], in10=func[4], in11=func[5], out=open
  or or_1 (out_11, lw, addu, ori, subu, lui, jal);
  or or_2 (out_9[0], addu, subu);
  buf or_3 (out_9[1], jal);  // OR_Gate
  or or_4 (out_8, lw, sw, ori, lui);
  buf or_5 (out_6, beq);  // OR_Gate
  buf or_6 (out_13[0], ori);  // OR_Gate
  buf or_7 (out_13[1], lui);  // OR_Gate
  or or_8 (out_16, j, jal);
  or or_9 (out_10, addu, ori, subu, beq, sw, lw);
  or or_10 (out_12, addu, subu, beq, sw);
  or or_11 (or_11_out, addu, subu);
  Multiplexer #(.width(4), .enable("false")) multiplexer_1 (
    .in0(4'b0000), .in1(4'b0001), .out(multiplexer_1_out), .sel(or_12_out));
  buf or_12 (or_12_out, jal);  // OR_Gate
  Multiplexer #(.width(2), .enable("false")) multiplexer_2 (
    .in0(2'b00), .in1(2'b01), .out(multiplexer_2_out), .sel(or_11_out));
  or or_13 (or_13_out, addu, ori, lui, subu);
  buf or_14 (out_5, sw);  // OR_Gate
  buf or_15 (out_3[0], lw);  // OR_Gate
  buf or_16 (out_3[1], jal);  // OR_Gate
  or or_17 (out_7[2], subu, beq);
  or or_18 (out_7[1], subu, lw, sw, addu, beq, lui, jal);
  buf or_19 (out_7[0], ori);  // OR_Gate
  Multiplexer #(.width(2), .enable("false")) multiplexer_3 (.in0(2'b00), .in1(2'b01), .out(out_14), .sel(or_20_out));
  or or_20 (or_20_out, addu, subu, ori, sw, lw);
  Multiplexer #(.width(2), .enable("false")) multiplexer_4 (
    .in0(multiplexer_2_out), .in1(2'b10), .out(out_15), .sel(sw));
  Multiplexer #(.width(4), .enable("false")) multiplexer_5 (
    .in0(multiplexer_1_out), .in1(4'b0010), .out(multiplexer_5_out), .sel(or_13_out));
  Multiplexer #(.width(4), .enable("false")) multiplexer_6 (
    .in0(multiplexer_5_out), .in1(4'b0100), .out(out_17), .sel(lw));

  assign out_4 = 1'b1;

  // Other names for the same wires on the sheet: ALUSrc = out_8; Branch = out_6; jump = out_16; MemWrite = out_5;
  //   MemtoReg0 = out_3[0]; MemtoReg1 = out_3[1]; ALUOp0 = out_7[0]; ALUOp1 = out_7[1]; ALUOp2 = out_7[2];
  //   RegDst0 = out_9[0]; RegDst1 = out_9[1]; ExtOp0 = out_13[0]; ExtOp1 = out_13[1]; RegWrite = out_11; s1 = out_10;
  //   s2 = out_12; tnew[3:0] = out_17; tuse1[1:0] = out_14; tuse2[1:0] = out_15
endmodule

module Spliter (
  input  [31:0] insturcture,
  output [5:0] Op,
  output [5:0] Func,
  output [25:0] instr_index,
  output [15:0] imme,
  output [4:0] rs,
  output [4:0] rt,
  output [4:0] rd,
  output [4:0] s
);


  assign Func = insturcture[5:0];
  assign imme = insturcture[15:0];
  assign instr_index = insturcture[25:0];
  assign Op = insturcture[31:26];
  assign rd = insturcture[15:11];
  assign rs = insturcture[25:21];
  assign rt = insturcture[20:16];
  assign s = insturcture[10:6];
endmodule

// EXT
module ext (
  input  [15:0] in_1,
  input  [1:0] extop,
  output [31:0] out_3
);

  wire [31:0] bit_extender_1_out, bit_extender_2_out, bit_extender_3_out, shifter_1_out;

  assign bit_extender_1_out = {{16{in_1[15]}}, in_1};  // Bit_Extender bit_extender_1
  assign bit_extender_2_out = {{16{1'b0}}, in_1};  // Bit_Extender bit_extender_2
  assign bit_extender_3_out = {{16{1'b0}}, in_1};  // Bit_Extender bit_extender_3
  Shifter #(.width(32)) shifter_1 (.in(bit_extender_3_out), .\dist (5'b10000), .out(shifter_1_out));
  Multiplexer #(.select(2), .width(32), .enable("false")) multiplexer_1 (
    .in0(bit_extender_1_out), .in1(bit_extender_2_out), .in2(shifter_1_out), .out(out_3), .sel(extop));  // open: in3
endmodule

module grf (
  input  [4:0] A1,
  input  clk,
  input  reset,
  input  we,
  input  [4:0] A2,
  input  [4:0] A3,
  input  [31:0] WD,
  output [31:0] RD1,
  output [31:0] RD2
);

  wire and_1_out, and_2_out, comparator_1_eq, comparator_2_eq, comparator_3_eq, comparator_4_eq;
  wire [31:0] I0, I1, I2, I3, I4, I5, I6, I7, I8, I9, I10, I11, I12, I13, I14, I15, I16, I17, I18, I19, I20,
       I21, I22, I23, I24, I25, I26, I27, I28, I29, I30, I31, multiplexer_2_out, multiplexer_3_out, O0, O1,
       O2, O3, O4, O5, O6, O7, O8, O9, O10, O11, O12, O13, O14, O15, O16, O17, O18, O19, O20, O21, O22, O23,
       O24, O25, O26, O27, O28, O29, O30, O31, RD1_t, RD2_t;

  Demultiplexer #(.select(5), .width(32), .tristate("true")) demultiplexer_1 (
    .out0(I0), .out1(I1), .out2(I2), .out3(I3), .out4(I4), .out5(I5), .out6(I6), .out7(I7), .out8(I8),
    .out9(I9), .out10(I10), .out11(I11), .out12(I12), .out13(I13), .out14(I14), .out15(I15), .out16(I16),
    .out17(I17), .out18(I18), .out19(I19), .out20(I20), .out21(I21), .out22(I22), .out23(I23), .out24(I24),
    .out25(I25), .out26(I26), .out27(I27), .out28(I28), .out29(I29), .out30(I30), .out31(I31), .in(WD),
    .sel(A3));  // open: en
  Comparator #(.width(5)) comparator_1 (.a(A1), .b(A3), .eq(comparator_1_eq));  // open: gt, lt
  Comparator #(.width(5)) comparator_2 (.a(A2), .b(A3), .eq(comparator_2_eq));  // open: gt, lt
  Multiplexer #(.select(5), .width(32)) multiplexer_1 (
    .in0(O0), .in1(O1), .in2(O2), .in3(O3), .in4(O4), .in5(O5), .in6(O6), .in7(O7), .in8(O8), .in9(O9),
    .in10(O10), .in11(O11), .in12(O12), .in13(O13), .in14(O14), .in15(O15), .in16(O16), .in17(O17),
    .in18(O18), .in19(O19), .in20(O20), .in21(O21), .in22(O22), .in23(O23), .in24(O24), .in25(O25),
    .in26(O26), .in27(O27), .in28(O28), .in29(O29), .in30(O30), .in31(O31), .out(RD2_t), .sel(A2));  // open: en
  Multiplexer #(.width(32), .enable("false")) multiplexer_2 (
    .in0(RD1_t), .in1(WD), .out(multiplexer_2_out), .sel(and_1_out));
  and and_1 (and_1_out, we, comparator_1_eq);
  and and_2 (and_2_out, we, comparator_2_eq);
  Multiplexer #(.width(32), .enable("false")) multiplexer_3 (
    .in0(RD2_t), .in1(WD), .out(multiplexer_3_out), .sel(and_2_out));
  Multiplexer #(.width(32), .enable("false")) multiplexer_4 (
    .in0(multiplexer_2_out), .in1({32{1'b0}}), .out(RD1), .sel(comparator_3_eq));
  Comparator #(.width(5)) comparator_3 (.a(A1), .b({5{1'b0}}), .eq(comparator_3_eq));  // open: gt, lt
  Multiplexer #(.width(32), .enable("false")) multiplexer_5 (
    .in0(multiplexer_3_out), .in1({32{1'b0}}), .out(RD2), .sel(comparator_4_eq));
  Comparator #(.width(5)) comparator_4 (.a(A2), .b({5{1'b0}}), .eq(comparator_4_eq));  // open: gt, lt
  Multiplexer #(.select(5), .width(32)) multiplexer_6 (
    .in0(O0), .in1(O1), .in2(O2), .in3(O3), .in4(O4), .in5(O5), .in6(O6), .in7(O7), .in8(O8), .in9(O9),
    .in10(O10), .in11(O11), .in12(O12), .in13(O13), .in14(O14), .in15(O15), .in16(O16), .in17(O17),
    .in18(O18), .in19(O19), .in20(O20), .in21(O21), .in22(O22), .in23(O23), .in24(O24), .in25(O25),
    .in26(O26), .in27(O27), .in28(O28), .in29(O29), .in30(O30), .in31(O31), .out(RD1_t), .sel(A1));  // open: en
  Register #(.width(32)) register_1 (.D({32{1'b0}}), .en(we), .Q(O0), .clk(clk), .clr(reset));
  Register #(.width(32)) register_2 (.D(I8), .en(we), .Q(O8), .clk(clk), .clr(reset));
  Register #(.width(32)) register_3 (.D(I16), .en(we), .Q(O16), .clk(clk), .clr(reset));
  Register #(.width(32)) register_4 (.D(I24), .en(we), .Q(O24), .clk(clk), .clr(reset));
  Register #(.width(32)) register_5 (.D(I1), .en(we), .Q(O1), .clk(clk), .clr(reset));
  Register #(.width(32)) register_6 (.D(I9), .en(we), .Q(O9), .clk(clk), .clr(reset));
  Register #(.width(32)) register_7 (.D(I17), .en(we), .Q(O17), .clk(clk), .clr(reset));
  Register #(.width(32)) register_8 (.D(I25), .en(we), .Q(O25), .clk(clk), .clr(reset));
  Register #(.width(32)) register_9 (.D(I2), .en(we), .Q(O2), .clk(clk), .clr(reset));
  Register #(.width(32)) register_10 (.D(I10), .en(we), .Q(O10), .clk(clk), .clr(reset));
  Register #(.width(32)) register_11 (.D(I18), .en(we), .Q(O18), .clk(clk), .clr(reset));
  Register #(.width(32)) register_12 (.D(I26), .en(we), .Q(O26), .clk(clk), .clr(reset));
  Register #(.width(32)) register_13 (.D(I3), .en(we), .Q(O3), .clk(clk), .clr(reset));
  Register #(.width(32)) register_14 (.D(I11), .en(we), .Q(O11), .clk(clk), .clr(reset));
  Register #(.width(32)) register_15 (.D(I19), .en(we), .Q(O19), .clk(clk), .clr(reset));
  Register #(.width(32)) register_16 (.D(I27), .en(we), .Q(O27), .clk(clk), .clr(reset));
  Register #(.width(32)) register_17 (.D(I4), .en(we), .Q(O4), .clk(clk), .clr(reset));
  Register #(.width(32)) register_18 (.D(I12), .en(we), .Q(O12), .clk(clk), .clr(reset));
  Register #(.width(32)) register_19 (.D(I20), .en(we), .Q(O20), .clk(clk), .clr(reset));
  Register #(.width(32)) register_20 (.D(I28), .en(we), .Q(O28), .clk(clk), .clr(reset));
  Register #(.width(32)) register_21 (.D(I5), .en(we), .Q(O5), .clk(clk), .clr(reset));
  Register #(.width(32)) register_22 (.D(I13), .en(we), .Q(O13), .clk(clk), .clr(reset));
  Register #(.width(32)) register_23 (.D(I21), .en(we), .Q(O21), .clk(clk), .clr(reset));
  Register #(.width(32)) register_24 (.D(I29), .en(we), .Q(O29), .clk(clk), .clr(reset));
  Register #(.width(32)) register_25 (.D(I6), .en(we), .Q(O6), .clk(clk), .clr(reset));
  Register #(.width(32)) register_26 (.D(I14), .en(we), .Q(O14), .clk(clk), .clr(reset));
  Register #(.width(32)) register_27 (.D(I22), .en(we), .Q(O22), .clk(clk), .clr(reset));
  Register #(.width(32)) register_28 (.D(I30), .en(we), .Q(O30), .clk(clk), .clr(reset));
  Register #(.width(32)) register_29 (.D(I7), .en(we), .Q(O7), .clk(clk), .clr(reset));
  Register #(.width(32)) register_30 (.D(I15), .en(we), .Q(O15), .clk(clk), .clr(reset));
  Register #(.width(32)) register_31 (.D(I23), .en(we), .Q(O23), .clk(clk), .clr(reset));
  Register #(.width(32)) register_32 (.D(I31), .en(we), .Q(O31), .clk(clk), .clr(reset));
endmodule

module forwardUnit (
  input  [4:0] s1_D,
  input  [4:0] s2_D,
  input  [4:0] s1_E,
  input  [4:0] s2_E,
  input  [4:0] des_E,
  input  [3:0] tNew_E,
  input  [4:0] s2_M,
  input  [3:0] tNew_M,
  input  [4:0] des_M,
  input  [3:0] tNew_W,
  input  [4:0] des_W,
  output [1:0] fRsDsel,
  output [1:0] fRtDsel,
  output [1:0] fRsEsel,
  output [1:0] fRtEsel,
  output fRtMsel
);

  wire and_1_out, and_2_out, and_3_out, and_4_out, and_5_out, and_6_out, and_7_out, and_8_out, and_9_out,
       comparator_1_eq, comparator_2_eq, comparator_3_eq, comparator_4_eq, comparator_5_eq, comparator_6_eq,
       comparator_7_eq, comparator_8_eq, comparator_9_eq, comparator_10_eq, comparator_11_eq,
       comparator_12_eq, comparator_13_eq, comparator_14_eq, comparator_15_eq, comparator_16_eq,
       comparator_17_eq, comparator_18_eq, comparator_19_eq, comparator_20_eq, comparator_21_eq,
       comparator_22_eq, comparator_23_eq, comparator_24_eq, comparator_25_eq, comparator_26_eq,
       comparator_27_eq, not_1_out, not_2_out, not_3_out, not_4_out, not_5_out, not_6_out, not_7_out,
       not_8_out, not_9_out;
  wire [1:0] multiplexer_1_out, multiplexer_2_out, multiplexer_5_out, multiplexer_6_out;

  Comparator #(.width(5), .mode("unsigned")) comparator_1 (
    .a(s1_D), .b({5{1'b0}}), .eq(comparator_1_eq));  // open: gt, lt
  not not_1 (not_1_out, comparator_1_eq);
  Comparator #(.width(5), .mode("unsigned")) comparator_2 (.a(s1_D), .b(des_M), .eq(comparator_2_eq));  // open: gt, lt
  Comparator #(.width(4), .mode("unsigned")) comparator_3 (
    .a(tNew_M), .b(4'b0000), .eq(comparator_3_eq));  // open: gt, lt
  not not_2 (not_2_out, comparator_4_eq);
  Comparator #(.width(5), .mode("unsigned")) comparator_4 (
    .a(s1_D), .b({5{1'b0}}), .eq(comparator_4_eq));  // open: gt, lt
  Comparator #(.width(5), .mode("unsigned")) comparator_5 (.a(s1_D), .b(des_E), .eq(comparator_5_eq));  // open: gt, lt
  Comparator #(.width(4), .mode("unsigned")) comparator_6 (
    .a(tNew_E), .b(4'b0000), .eq(comparator_6_eq));  // open: gt, lt
  Comparator #(.width(5), .mode("unsigned")) comparator_7 (
    .a(s2_D), .b({5{1'b0}}), .eq(comparator_7_eq));  // open: gt, lt
  Comparator #(.width(5), .mode("unsigned")) comparator_8 (.a(s2_D), .b(des_M), .eq(comparator_8_eq));  // open: gt, lt
  Comparator #(.width(4), .mode("unsigned")) comparator_9 (
    .a(tNew_M), .b(4'b0000), .eq(comparator_9_eq));  // open: gt, lt
  Comparator #(.width(5), .mode("unsigned")) comparator_10 (
    .a(s2_D), .b({5{1'b0}}), .eq(comparator_10_eq));  // open: gt, lt
  Comparator #(.width(5), .mode("unsigned")) comparator_11 (
    .a(s2_D), .b(des_E), .eq(comparator_11_eq));  // open: gt, lt
  Comparator #(.width(4), .mode("unsigned")) comparator_12 (
    .a(tNew_E), .b(4'b0000), .eq(comparator_12_eq));  // open: gt, lt
  and and_1 (and_1_out, not_1_out, comparator_2_eq, comparator_3_eq);
  and and_2 (and_2_out, not_2_out, comparator_5_eq, comparator_6_eq);
  not not_3 (not_3_out, comparator_7_eq);
  not not_4 (not_4_out, comparator_10_eq);
  Multiplexer #(.width(2)) multiplexer_1 (
    .in0(2'b00), .in1(2'b10), .out(multiplexer_1_out), .sel(and_1_out));  // open: en
  and and_3 (and_3_out, not_3_out, comparator_8_eq, comparator_9_eq);
  and and_4 (and_4_out, not_4_out, comparator_11_eq, comparator_12_eq);
  Multiplexer #(.width(2)) multiplexer_2 (
    .in0(2'b00), .in1(2'b10), .out(multiplexer_2_out), .sel(and_3_out));  // open: en
  Multiplexer #(.width(2)) multiplexer_3 (
    .in0(multiplexer_1_out), .in1(2'b01), .out(fRsDsel), .sel(and_2_out));  // open: en
  Multiplexer #(.width(2)) multiplexer_4 (
    .in0(multiplexer_2_out), .in1(2'b01), .out(fRtDsel), .sel(and_4_out));  // open: en
  Comparator #(.width(5), .mode("unsigned")) comparator_13 (
    .a(s1_E), .b({5{1'b0}}), .eq(comparator_13_eq));  // open: gt, lt
  Comparator #(.width(5), .mode("unsigned")) comparator_14 (
    .a(s1_E), .b(des_W), .eq(comparator_14_eq));  // open: gt, lt
  Comparator #(.width(4), .mode("unsigned")) comparator_15 (
    .a(tNew_W), .b(4'b0000), .eq(comparator_15_eq));  // open: gt, lt
  Comparator #(.width(5), .mode("unsigned")) comparator_16 (
    .a(s1_E), .b({5{1'b0}}), .eq(comparator_16_eq));  // open: gt, lt
  Comparator #(.width(5), .mode("unsigned")) comparator_17 (
    .a(s1_E), .b(des_M), .eq(comparator_17_eq));  // open: gt, lt
  Comparator #(.width(4), .mode("unsigned")) comparator_18 (
    .a(tNew_M), .b(4'b0000), .eq(comparator_18_eq));  // open: gt, lt
  Comparator #(.width(5), .mode("unsigned")) comparator_19 (
    .a(s2_E), .b({5{1'b0}}), .eq(comparator_19_eq));  // open: gt, lt
  Comparator #(.width(5), .mode("unsigned")) comparator_20 (
    .a(s2_E), .b(des_W), .eq(comparator_20_eq));  // open: gt, lt
  Comparator #(.width(4), .mode("unsigned")) comparator_21 (
    .a(tNew_W), .b(4'b0000), .eq(comparator_21_eq));  // open: gt, lt
  Comparator #(.width(5), .mode("unsigned")) comparator_22 (
    .a(s2_E), .b({5{1'b0}}), .eq(comparator_22_eq));  // open: gt, lt
  Comparator #(.width(5), .mode("unsigned")) comparator_23 (
    .a(s2_E), .b(des_M), .eq(comparator_23_eq));  // open: gt, lt
  Comparator #(.width(4), .mode("unsigned")) comparator_24 (
    .a(tNew_M), .b(4'b0000), .eq(comparator_24_eq));  // open: gt, lt
  not not_5 (not_5_out, comparator_13_eq);
  not not_6 (not_6_out, comparator_16_eq);
  not not_7 (not_7_out, comparator_19_eq);
  not not_8 (not_8_out, comparator_22_eq);
  and and_5 (and_5_out, not_5_out, comparator_14_eq, comparator_15_eq);
  and and_6 (and_6_out, not_6_out, comparator_17_eq, comparator_18_eq);
  and and_7 (and_7_out, not_7_out, comparator_20_eq, comparator_21_eq);
  and and_8 (and_8_out, not_8_out, comparator_23_eq, comparator_24_eq);
  Multiplexer #(.width(2)) multiplexer_5 (
    .in0(2'b00), .in1(2'b10), .out(multiplexer_5_out), .sel(and_5_out));  // open: en
  Multiplexer #(.width(2)) multiplexer_6 (
    .in0(2'b00), .in1(2'b10), .out(multiplexer_6_out), .sel(and_7_out));  // open: en
  Multiplexer #(.width(2)) multiplexer_7 (
    .in0(multiplexer_5_out), .in1(2'b01), .out(fRsEsel), .sel(and_6_out));  // open: en
  Multiplexer #(.width(2)) multiplexer_8 (
    .in0(multiplexer_6_out), .in1(2'b01), .out(fRtEsel), .sel(and_8_out));  // open: en
  not not_9 (not_9_out, comparator_25_eq);
  Comparator #(.width(5), .mode("unsigned")) comparator_25 (
    .a(s2_M), .b({5{1'b0}}), .eq(comparator_25_eq));  // open: gt, lt
  Comparator #(.width(5), .mode("unsigned")) comparator_26 (
    .a(s2_M), .b(des_W), .eq(comparator_26_eq));  // open: gt, lt
  Comparator #(.width(4), .mode("unsigned")) comparator_27 (
    .a(tNew_W), .b(4'b0000), .eq(comparator_27_eq));  // open: gt, lt
  and and_9 (and_9_out, not_9_out, comparator_26_eq, comparator_27_eq);
  Multiplexer multiplexer_9 (.in0(1'b0), .in1(1'b1), .out(fRtMsel), .sel(and_9_out));  // open: en
endmodule

module stall (
  input  [4:0] s1_D,
  input  [4:0] s2_D,
  input  [1:0] tUse1_D,
  input  [1:0] tUse2_D,
  input  [4:0] des_E,
  input  [3:0] tNew_E,
  input  [3:0] tNew_M,
  input  [4:0] des_M,
  output Stall_F,
  output Stall_D,
  output flush_E
);

  wire and_1_out, and_2_out, and_3_out, and_4_out, comparator_1_eq, comparator_2_eq, comparator_3_lt,
       comparator_4_eq, comparator_5_eq, comparator_6_lt, comparator_7_eq, comparator_8_eq, comparator_9_lt,
       comparator_10_eq, comparator_11_eq, comparator_12_lt, not_1_out, not_2_out, not_3_out, not_4_out;
  wire [3:0] tUse1_D_t, tUse2_D_t;

  Comparator #(.width(5), .mode("unsigned")) comparator_1 (
    .a(s1_D), .b({5{1'b0}}), .eq(comparator_1_eq));  // open: gt, lt
  Comparator #(.width(5), .mode("unsigned")) comparator_2 (.a(s1_D), .b(des_E), .eq(comparator_2_eq));  // open: gt, lt
  Comparator #(.width(4), .mode("unsigned")) comparator_3 (
    .a(tUse1_D_t), .b(tNew_E), .lt(comparator_3_lt));  // open: gt, eq
  Comparator #(.width(5), .mode("unsigned")) comparator_4 (
    .a(s2_D), .b({5{1'b0}}), .eq(comparator_4_eq));  // open: gt, lt
  Comparator #(.width(5), .mode("unsigned")) comparator_5 (.a(s2_D), .b(des_E), .eq(comparator_5_eq));  // open: gt, lt
  Comparator #(.width(4), .mode("unsigned")) comparator_6 (
    .a(tUse2_D_t), .b(tNew_E), .lt(comparator_6_lt));  // open: gt, eq
  Comparator #(.width(5), .mode("unsigned")) comparator_7 (
    .a(s1_D), .b({5{1'b0}}), .eq(comparator_7_eq));  // open: gt, lt
  Comparator #(.width(5), .mode("unsigned")) comparator_8 (.a(s1_D), .b(des_M), .eq(comparator_8_eq));  // open: gt, lt
  Comparator #(.width(4), .mode("unsigned")) comparator_9 (
    .a(tUse1_D_t), .b(tNew_M), .lt(comparator_9_lt));  // open: gt, eq
  Comparator #(.width(5), .mode("unsigned")) comparator_10 (
    .a(s2_D), .b({5{1'b0}}), .eq(comparator_10_eq));  // open: gt, lt
  Comparator #(.width(5), .mode("unsigned")) comparator_11 (
    .a(s2_D), .b(des_M), .eq(comparator_11_eq));  // open: gt, lt
  Comparator #(.width(4), .mode("unsigned")) comparator_12 (
    .a(tUse2_D_t), .b(tNew_M), .lt(comparator_12_lt));  // open: gt, eq
  assign tUse1_D_t = {{2{1'b0}}, tUse1_D};  // Bit_Extender bit_extender_1
  not not_1 (not_1_out, comparator_1_eq);
  not not_2 (not_2_out, comparator_4_eq);
  not not_3 (not_3_out, comparator_7_eq);
  not not_4 (not_4_out, comparator_10_eq);
  and and_1 (and_1_out, not_1_out, comparator_2_eq, comparator_3_lt);
  and and_2 (and_2_out, not_2_out, comparator_5_eq, comparator_6_lt);
  and and_3 (and_3_out, not_3_out, comparator_8_eq, comparator_9_lt);
  and and_4 (and_4_out, not_4_out, comparator_11_eq, comparator_12_lt);
  assign tUse2_D_t = {{2{1'b0}}, tUse2_D};  // Bit_Extender bit_extender_2
  or or_1 (flush_E, and_1_out, and_2_out, and_3_out, and_4_out);

  assign Stall_D = flush_E;
  assign Stall_F = flush_E;

  // Other names for the same wires on the sheet: stall_flag = flush_E
endmodule

module FDreg (
  input  in_1,
  input  in_2,
  input  [31:0] instr_i,
  input  [31:0] pc_i,
  input  in_5,
  output [31:0] instr_o,
  output [31:0] pc_o,
  output [31:0] pc_o_2,
  output [31:0] pc_o_3
);

  wire clk_prime, not_1_out, not_2_out;

  not not_1 (not_1_out, in_5);
  not not_2 (not_2_out, in_5);
  buf and_1 (clk_prime, in_1);  // AND_Gate
  Register #(.width(32)) register_1 (.D(instr_i), .en(not_1_out), .Q(instr_o), .clk(clk_prime), .clr(in_2));
  Register #(.width(32)) register_2 (.D(pc_i), .en(not_2_out), .Q(pc_o), .clk(clk_prime), .clr(in_2));
  Adder #(.width(32)) adder_1 (.a(pc_o), .b(32'h4), .out(pc_o_2));  // open: cin, cout
  Adder #(.width(32)) adder_2 (.a(pc_o_2), .b(32'h4), .out(pc_o_3));  // open: cin, cout

  // Other names for the same wires on the sheet: clk = in_1; F_D_stall = in_5; reset = in_2
endmodule

module DEreg (
  input  in_1,
  input  in_2,
  input  [1:0] regdst,
  input  regwrite,
  input  alusrc,
  input  memread,
  input  memwrite,
  input  [1:0] memtoreg,
  input  [2:0] aluop,
  input  [31:0] RD1_i,
  input  [31:0] RD2_i,
  input  [4:0] rs_i,
  input  in_13,
  input  [4:0] rt_i,
  input  [4:0] rd_i,
  input  [31:0] pc_i,
  input  [31:0] pc_4_i,
  input  [31:0] pc_8_i,
  input  [31:0] extres,
  input  [31:0] instr_i,
  input  [3:0] tnew,
  input  [4:0] s1,
  input  [4:0] s1_2,
  output [1:0] rs_o,
  output rs_o_2,
  output rs_o_3,
  output rs_o_4,
  output rs_o_5,
  output [1:0] rs_o_6,
  output [2:0] rs_o_7,
  output [31:0] RD1_o,
  output [31:0] RD2_o,
  output [4:0] rs_o_8,
  output [4:0] rt_o,
  output [4:0] rd_o,
  output [31:0] pc_o,
  output [31:0] pc_4_o,
  output [31:0] pc_8_o,
  output [31:0] extres_2,
  output [31:0] out_40,
  output [3:0] tnew_2,
  output [4:0] s1_3,
  output [4:0] s1_4
);

  wire multiplexer_2_out, multiplexer_3_out, multiplexer_4_out, multiplexer_5_out;
  wire [1:0] multiplexer_1_out, multiplexer_6_out;
  wire [2:0] multiplexer_7_out;
  wire [3:0] multiplexer_18_out, shifter_1_out;
  wire [4:0] multiplexer_10_out, multiplexer_11_out, multiplexer_12_out, multiplexer_19_out,
       multiplexer_20_out;
  wire [31:0] multiplexer_8_out, multiplexer_9_out, multiplexer_13_out, multiplexer_14_out,
       multiplexer_15_out, multiplexer_16_out, multiplexer_17_out;

  Shifter #(.width(4), .shift("lr")) shifter_1 (.in(tnew), .\dist (2'b01), .out(shifter_1_out));
  Multiplexer #(.width(2), .enable("false")) multiplexer_1 (
    .in0(regdst), .in1(2'b00), .out(multiplexer_1_out), .sel(in_13));
  Multiplexer #(.enable("false")) multiplexer_2 (.in0(regwrite), .in1(1'b0), .out(multiplexer_2_out), .sel(in_13));
  Multiplexer #(.enable("false")) multiplexer_3 (.in0(alusrc), .in1(1'b0), .out(multiplexer_3_out), .sel(in_13));
  Multiplexer #(.enable("false")) multiplexer_4 (.in0(memread), .in1(1'b0), .out(multiplexer_4_out), .sel(in_13));
  Multiplexer #(.enable("false")) multiplexer_5 (.in0(memwrite), .in1(1'b0), .out(multiplexer_5_out), .sel(in_13));
  Multiplexer #(.width(2), .enable("false")) multiplexer_6 (
    .in0(memtoreg), .in1(2'b00), .out(multiplexer_6_out), .sel(in_13));
  Multiplexer #(.width(3), .enable("false")) multiplexer_7 (
    .in0(aluop), .in1(3'b000), .out(multiplexer_7_out), .sel(in_13));
  Multiplexer #(.width(32), .enable("false")) multiplexer_8 (
    .in0(RD1_i), .in1({32{1'b0}}), .out(multiplexer_8_out), .sel(in_13));
  Multiplexer #(.width(32), .enable("false")) multiplexer_9 (
    .in0(RD2_i), .in1({32{1'b0}}), .out(multiplexer_9_out), .sel(in_13));
  Multiplexer #(.width(5), .enable("false")) multiplexer_10 (
    .in0(rs_i), .in1({5{1'b0}}), .out(multiplexer_10_out), .sel(in_13));
  Multiplexer #(.width(5), .enable("false")) multiplexer_11 (
    .in0(rt_i), .in1({5{1'b0}}), .out(multiplexer_11_out), .sel(in_13));
  Multiplexer #(.width(5), .enable("false")) multiplexer_12 (
    .in0(rd_i), .in1({5{1'b0}}), .out(multiplexer_12_out), .sel(in_13));
  Multiplexer #(.width(32), .enable("false")) multiplexer_13 (
    .in0(pc_i), .in1({32{1'b0}}), .out(multiplexer_13_out), .sel(in_13));
  Multiplexer #(.width(32), .enable("false")) multiplexer_14 (
    .in0(pc_4_i), .in1({32{1'b0}}), .out(multiplexer_14_out), .sel(in_13));
  Multiplexer #(.width(32), .enable("false")) multiplexer_15 (
    .in0(pc_8_i), .in1({32{1'b0}}), .out(multiplexer_15_out), .sel(in_13));
  Multiplexer #(.width(32), .enable("false")) multiplexer_16 (
    .in0(extres), .in1({32{1'b0}}), .out(multiplexer_16_out), .sel(in_13));
  Multiplexer #(.width(32), .enable("false")) multiplexer_17 (
    .in0(instr_i), .in1({32{1'b0}}), .out(multiplexer_17_out), .sel(in_13));
  Multiplexer #(.width(4), .enable("false")) multiplexer_18 (
    .in0(shifter_1_out), .in1(4'b0000), .out(multiplexer_18_out), .sel(in_13));
  Multiplexer #(.width(5), .enable("false")) multiplexer_19 (
    .in0(s1), .in1({5{1'b0}}), .out(multiplexer_19_out), .sel(in_13));
  Multiplexer #(.width(5), .enable("false")) multiplexer_20 (
    .in0(s1_2), .in1({5{1'b0}}), .out(multiplexer_20_out), .sel(in_13));
  Register #(.width(2)) register_1 (.D(multiplexer_1_out), .Q(rs_o), .clk(in_1), .clr(in_2));  // open: en
  Register #(.width(1)) register_2 (.D(multiplexer_2_out), .Q(rs_o_2), .clk(in_1), .clr(in_2));  // open: en
  Register #(.width(1)) register_3 (.D(multiplexer_3_out), .Q(rs_o_3), .clk(in_1), .clr(in_2));  // open: en
  Register #(.width(1)) register_4 (.D(multiplexer_4_out), .Q(rs_o_4), .clk(in_1), .clr(in_2));  // open: en
  Register #(.width(1)) register_5 (.D(multiplexer_5_out), .Q(rs_o_5), .clk(in_1), .clr(in_2));  // open: en
  Register #(.width(2)) register_6 (.D(multiplexer_6_out), .Q(rs_o_6), .clk(in_1), .clr(in_2));  // open: en
  Register #(.width(3)) register_7 (.D(multiplexer_7_out), .Q(rs_o_7), .clk(in_1), .clr(in_2));  // open: en
  Register #(.width(32)) register_8 (.D(multiplexer_8_out), .Q(RD1_o), .clk(in_1), .clr(in_2));  // open: en
  Register #(.width(32)) register_9 (.D(multiplexer_9_out), .Q(RD2_o), .clk(in_1), .clr(in_2));  // open: en
  Register #(.width(5)) register_10 (.D(multiplexer_10_out), .Q(rs_o_8), .clk(in_1), .clr(in_2));  // open: en
  Register #(.width(5)) register_11 (.D(multiplexer_11_out), .Q(rt_o), .clk(in_1), .clr(in_2));  // open: en
  Register #(.width(5)) register_12 (.D(multiplexer_12_out), .Q(rd_o), .clk(in_1), .clr(in_2));  // open: en
  Register #(.width(32)) register_13 (.D(multiplexer_13_out), .Q(pc_o), .clk(in_1), .clr(in_2));  // open: en
  Register #(.width(32)) register_14 (.D(multiplexer_14_out), .Q(pc_4_o), .clk(in_1), .clr(in_2));  // open: en
  Register #(.width(32)) register_15 (.D(multiplexer_17_out), .Q(out_40), .clk(in_1), .clr(in_2));  // open: en
  Register #(.width(4)) register_16 (.D(multiplexer_18_out), .Q(tnew_2), .clk(in_1), .clr(in_2));  // open: en
  Register #(.width(5)) register_17 (.D(multiplexer_19_out), .Q(s1_3), .clk(in_1), .clr(in_2));  // open: en
  Register #(.width(5)) register_18 (.D(multiplexer_20_out), .Q(s1_4), .clk(in_1), .clr(in_2));  // open: en
  Register #(.width(32)) register_19 (.D(multiplexer_15_out), .Q(pc_8_o), .clk(in_1), .clr(in_2));  // open: en
  Register #(.width(32)) register_20 (.D(multiplexer_16_out), .Q(extres_2), .clk(in_1), .clr(in_2));  // open: en

  // Other names for the same wires on the sheet: clk = in_1; clk_prime = in_1; flush = in_13; Reset = in_2
endmodule

module EMreg (
  input  in_1,
  input  in_2,
  input  memwrite,
  input  regwrite,
  input  memread,
  input  [1:0] memtoreg,
  input  [31:0] aluresult_i,
  input  [31:0] writedata_i,
  input  [4:0] writereg_i,
  input  [31:0] pc_i,
  input  [31:0] pc_4_i,
  input  [31:0] pc_8_i,
  input  [31:0] instr_i,
  input  [3:0] tnew,
  input  [4:0] s2,
  output out_16,
  output out_17,
  output out_18,
  output [1:0] out_19,
  output [31:0] out_20,
  output [31:0] out_21,
  output [4:0] out_22,
  output [31:0] pc_o,
  output [31:0] pc_4_o,
  output [31:0] pc_8_o,
  output [31:0] out_26,
  output [3:0] out_27,
  output [4:0] out_28
);

  wire [3:0] shifter_1_out;

  Shifter #(.width(4), .shift("lr")) shifter_1 (.in(tnew), .\dist (2'b01), .out(shifter_1_out));
  Register #(.width(1)) register_1 (.D(memwrite), .Q(out_16), .clk(in_1), .clr(in_2));  // open: en
  Register #(.width(1)) register_2 (.D(regwrite), .Q(out_17), .clk(in_1), .clr(in_2));  // open: en
  Register #(.width(1)) register_3 (.D(memread), .Q(out_18), .clk(in_1), .clr(in_2));  // open: en
  Register #(.width(2)) register_4 (.D(memtoreg), .Q(out_19), .clk(in_1), .clr(in_2));  // open: en
  Register #(.width(32)) register_5 (.D(aluresult_i), .Q(out_20), .clk(in_1), .clr(in_2));  // open: en
  Register #(.width(32)) register_6 (.D(writedata_i), .Q(out_21), .clk(in_1), .clr(in_2));  // open: en
  Register #(.width(5)) register_7 (.D(writereg_i), .Q(out_22), .clk(in_1), .clr(in_2));  // open: en
  Register #(.width(32)) register_8 (.D(pc_i), .Q(pc_o), .clk(in_1), .clr(in_2));  // open: en
  Register #(.width(32)) register_9 (.D(pc_4_i), .Q(pc_4_o), .clk(in_1), .clr(in_2));  // open: en
  Register #(.width(32)) register_10 (.D(pc_8_i), .Q(pc_8_o), .clk(in_1), .clr(in_2));  // open: en
  Register #(.width(32)) register_11 (.D(instr_i), .Q(out_26), .clk(in_1), .clr(in_2));  // open: en
  Register #(.width(4)) register_12 (.D(shifter_1_out), .Q(out_27), .clk(in_1), .clr(in_2));  // open: en
  Register #(.width(5)) register_13 (.D(s2), .Q(out_28), .clk(in_1), .clr(in_2));  // open: en

  // Other names for the same wires on the sheet: clk = in_1; clk_prime = in_1; Reset = in_2
endmodule

module MWreg (
  input  in_1,
  input  in_2,
  input  memwrite,
  input  [1:0] memwrite_2,
  input  [31:0] aluresult_i,
  input  [31:0] writedata_i,
  input  [31:0] readdata_i,
  input  [31:0] pc_i,
  input  [31:0] pc_4_i,
  input  [31:0] pc_8_i,
  input  [31:0] instr_i,
  input  [4:0] writereg_i,
  input  [31:0] memaddr,
  input  [31:0] memdata,
  input  memwrite_3,
  input  [3:0] tnew,
  output out_17,
  output [1:0] out_18,
  output [31:0] out_19,
  output [31:0] out_20,
  output [31:0] out_21,
  output [31:0] pc_o,
  output [31:0] pc_4_o,
  output [31:0] pc_8_o,
  output [31:0] out_25,
  output [4:0] out_26,
  output [31:0] out_27,
  output [31:0] out_28,
  output out_29,
  output [3:0] out_30
);

  wire [3:0] shifter_1_out;

  Shifter #(.width(4), .shift("lr")) shifter_1 (.in(tnew), .\dist (2'b01), .out(shifter_1_out));
  Register #(.width(1)) register_1 (.D(memwrite), .Q(out_17), .clk(in_1), .clr(in_2));  // open: en
  Register #(.width(2)) register_2 (.D(memwrite_2), .Q(out_18), .clk(in_1), .clr(in_2));  // open: en
  Register #(.width(32)) register_3 (.D(aluresult_i), .Q(out_19), .clk(in_1), .clr(in_2));  // open: en
  Register #(.width(32)) register_4 (.D(writedata_i), .Q(out_20), .clk(in_1), .clr(in_2));  // open: en
  Register #(.width(32)) register_5 (.D(readdata_i), .Q(out_21), .clk(in_1), .clr(in_2));  // open: en
  Register #(.width(32)) register_6 (.D(pc_i), .Q(pc_o), .clk(in_1), .clr(in_2));  // open: en
  Register #(.width(32)) register_7 (.D(pc_4_i), .Q(pc_4_o), .clk(in_1), .clr(in_2));  // open: en
  Register #(.width(32)) register_8 (.D(pc_8_i), .Q(pc_8_o), .clk(in_1), .clr(in_2));  // open: en
  Register #(.width(32)) register_9 (.D(instr_i), .Q(out_25), .clk(in_1), .clr(in_2));  // open: en
  Register #(.width(5)) register_10 (.D(writereg_i), .Q(out_26), .clk(in_1), .clr(in_2));  // open: en
  Register #(.width(32)) register_11 (.D(memaddr), .Q(out_27), .clk(in_1), .clr(in_2));  // open: en
  Register #(.width(32)) register_12 (.D(memdata), .Q(out_28), .clk(in_1), .clr(in_2));  // open: en
  Register #(.width(1)) register_13 (.D(memwrite_3), .Q(out_29), .clk(in_1), .clr(in_2));  // open: en
  Register #(.width(4)) register_14 (.D(shifter_1_out), .Q(out_30), .clk(in_1), .clr(in_2));  // open: en

  // Other names for the same wires on the sheet: clk = in_1; clk_prime = in_1; Reset = in_2
endmodule

module IFU (
  input  in_1,
  input  in_2,
  input  [31:0] pc_i,
  input  in_4,
  output [9:0] instr_o,
  output [31:0] pc_o
);

  wire clk_prime, comparator_1_eq, not_1_out;
  wire [31:0] register_1_q, shifter_1_out;

  not not_1 (not_1_out, in_4);
  Register #(.width(32)) register_1 (.D(pc_i), .en(not_1_out), .Q(register_1_q), .clk(clk_prime), .clr(in_2));
  buf and_1 (clk_prime, in_1);  // AND_Gate
  Comparator #(.width(32)) comparator_1 (.a(register_1_q), .b({32{1'b0}}), .eq(comparator_1_eq));  // open: gt, lt
  Shifter #(.width(32), .shift("lr")) shifter_1 (.in(pc_o), .\dist (5'b00010), .out(shifter_1_out));
  Multiplexer #(.width(32), .enable("false")) multiplexer_1 (
    .in0(register_1_q), .in1(32'h3000), .out(pc_o), .sel(comparator_1_eq));
  Bit_Extender #(.in_width(32), .out_width(10)) bit_extender_1 (.in(shifter_1_out), .out(instr_o));

  // Other names for the same wires on the sheet: clk = in_1; F_D_stall = in_4; reset = in_2
endmodule

module NPC (
  input  beq,
  input  jump,
  input  jr,
  input  equ,
  input  [31:0] pc,
  input  [31:0] branchaddr,
  input  [25:0] imme26,
  input  [31:0] reg31,
  output [31:0] npc
);

  wire and_2_out;
  wire [31:0] adder_1_out, adder_2_out, and_1_out, bit_extender_1_out, multiplexer_1_out, multiplexer_3_out,
       or_1_out, shifter_1_out, shifter_2_out;

  Shifter #(.width(32)) shifter_1 (.in(branchaddr), .\dist (5'b00010), .out(shifter_1_out));
  assign and_1_out = pc & 32'hf0000000;  // AND_Gate and_1, 32 bits wide
  assign bit_extender_1_out = {{6{1'b0}}, imme26};  // Bit_Extender bit_extender_1
  Adder #(.width(32)) adder_1 (.a(pc), .b(32'h4), .out(adder_1_out));  // open: cin, cout
  Adder #(.width(32)) adder_2 (.a(pc), .b(shifter_1_out), .out(adder_2_out));  // open: cin, cout
  Shifter #(.width(32)) shifter_2 (.in(bit_extender_1_out), .\dist (5'b00010), .out(shifter_2_out));
  Multiplexer #(.width(32), .enable("false")) multiplexer_1 (
    .in0(adder_1_out), .in1(adder_2_out), .out(multiplexer_1_out), .sel(and_2_out));
  and and_2 (and_2_out, beq, equ);
  assign or_1_out = and_1_out | shifter_2_out;  // OR_Gate or_1, 32 bits wide
  Multiplexer #(.width(32), .enable("false")) multiplexer_2 (
    .in0(multiplexer_1_out), .in1(or_1_out), .out(npc), .sel(jump));
  Multiplexer #(.width(32), .enable("false")) multiplexer_3 (
    .in1(reg31), .out(multiplexer_3_out), .sel(jr));  // open: in0

  // Other names for the same wires on the sheet: jal = jump
endmodule
