// Logisim project p5.circ as structural Verilog: 6 circuits, main circuit Cache
module Cache (
  input  [31:0] in_1,
  input  [31:0] in_2,
  input  in_3,
  input  in_4,
  input  in_5,
  input  in_6,
  output [15:0] out_7,
  output [15:0] out_8,
  output out_9,
  output [31:0] out_10
);

  wire and_1_out, and_2_out, en1, en2, en3, en4, hit, hit1, hit2, hit3, hit4, or_1_out, or_3_out;
  wire [31:0] d1, d2, d3, d4, g1_out_12, g1_out_13, g1_out_14, g1_out_15, g2_out_12, g2_out_13, g2_out_14,
       g2_out_15, g3_out_12, g3_out_13, g3_out_14, g3_out_15, g4_out_12, g4_out_13, g4_out_14, g4_out_15,
       multiplexer_1_out, multiplexer_2_out, multiplexer_3_out, multiplexer_4_out, multiplexer_5_out, out1,
       out2, out3, out4;

  and and_1 (and_1_out, in_5, ~out_9);  // AND_Gate
  and and_2 (and_2_out, in_5, ~out_9, hit);  // AND_Gate
  Counter #(.width(16), .max('hffff)) counter_1 (
    .count(and_1_out), .Q(out_7), .clk(in_4), .clr(in_6));  // open: load, D, carry
  Counter #(.width(16), .max('hffff)) counter_2 (
    .count(and_2_out), .Q(out_8), .clk(in_4), .clr(in_6));  // open: load, D, carry
  ram ram_1 (
    .MuxBlock(in_1[3:2]), .MemWrite(in_3), .MemRead(in_5), .Hit(hit), .Tag(in_1[11:6]), .MuxGroup(in_1[5:4]),
    .MemData(in_2), .Clk(in_4), .Reset(in_6), ._4(d4), ._3(d3), ._2(d2), .out_13(out_9), ._1(d1));
  or or_1 (or_1_out, in_3, in_5);
  Demultiplexer #(.select(2)) demultiplexer_1 (
    .out0(en1), .out1(en2), .out2(en3), .out3(en4), .in(or_1_out), .sel(in_1[5:4]));  // open: en
  or or_2 (hit, hit1, hit2, hit3, hit4);
  Multiplexer #(.select(2), .width(32)) multiplexer_1 (
    .in0(d1), .in1(d2), .in2(d3), .in3(d4), .out(multiplexer_1_out), .sel(in_1[3:2]));  // open: en
  Multiplexer #(.width(32)) multiplexer_2 (
    .in0(multiplexer_1_out), .in1(out1), .out(multiplexer_2_out), .sel(hit1));  // open: en
  Multiplexer #(.width(32)) multiplexer_3 (
    .in0(multiplexer_2_out), .in1(out2), .out(multiplexer_3_out), .sel(hit2));  // open: en
  group g1 (
    .in_5(in_4), .in_6(in_6), .tag(in_1[11:6]), .in_10(out_9), .in_11(en1), .out_12(g1_out_12),
    .out_13(g1_out_13), .out_14(g1_out_14), .out_15(g1_out_15), .in_1(d1), .in_2(d2), .in_3(d3), .in_4(d4),
    .in_8(in_5), .in_9(in_3), .out_16(hit1));
  group g2 (
    .in_5(in_4), .in_6(in_6), .tag(in_1[11:6]), .in_10(out_9), .in_11(en2), .out_12(g2_out_12),
    .out_13(g2_out_13), .out_14(g2_out_14), .out_15(g2_out_15), .in_1(d1), .in_2(d2), .in_3(d3), .in_4(d4),
    .in_8(in_5), .in_9(in_3), .out_16(hit2));
  group g3 (
    .in_5(in_4), .in_6(in_6), .tag(in_1[11:6]), .in_10(out_9), .in_11(en3), .out_12(g3_out_12),
    .out_13(g3_out_13), .out_14(g3_out_14), .out_15(g3_out_15), .in_1(d1), .in_2(d2), .in_3(d3), .in_4(d4),
    .in_8(in_5), .in_9(in_3), .out_16(hit3));
  group g4 (
    .in_5(in_4), .in_6(in_6), .tag(in_1[11:6]), .in_10(out_9), .in_11(en4), .out_12(g4_out_12),
    .out_13(g4_out_13), .out_14(g4_out_14), .out_15(g4_out_15), .in_1(d1), .in_2(d2), .in_3(d3), .in_4(d4),
    .in_8(in_5), .in_9(in_3), .out_16(hit4));
  Multiplexer #(.width(32)) multiplexer_4 (
    .in0(multiplexer_3_out), .in1(out3), .out(multiplexer_4_out), .sel(hit3));  // open: en
  Multiplexer #(.width(32)) multiplexer_5 (
    .in0(multiplexer_4_out), .in1(out4), .out(multiplexer_5_out), .sel(hit4));  // open: en
  or or_3 (or_3_out, out_9, in_3);
  Multiplexer #(.width(32)) multiplexer_6 (
    .in0(multiplexer_5_out), .in1({32{1'b0}}), .out(out_10), .sel(or_3_out));  // open: en
  Multiplexer #(.select(2), .width(32)) multiplexer_7 (
    .in0(g1_out_12), .in1(g1_out_13), .in2(g1_out_14), .in3(g1_out_15), .out(out1), .sel(in_1[3:2]));  // open: en
  Multiplexer #(.select(2), .width(32)) multiplexer_8 (
    .in0(g2_out_12), .in1(g2_out_13), .in2(g2_out_14), .in3(g2_out_15), .out(out2), .sel(in_1[3:2]));  // open: en
  Multiplexer #(.select(2), .width(32)) multiplexer_9 (
    .in0(g3_out_12), .in1(g3_out_13), .in2(g3_out_14), .in3(g3_out_15), .out(out3), .sel(in_1[3:2]));  // open: en
  Multiplexer #(.select(2), .width(32)) multiplexer_10 (
    .in0(g4_out_12), .in1(g4_out_13), .in2(g4_out_14), .in3(g4_out_15), .out(out4), .sel(in_1[3:2]));  // open: en

  // Other names for the same wires on the sheet: clk = in_4; MuxBlock[1:0] = in_1[3:2]; MuxGroup[1:0] = in_1[5:4];
  //   tag[5:0] = in_1[11:6]; MemRead = in_5; MemWrite = in_3; rst = in_6; stop = out_9
endmodule

module group (
  input  [31:0] in_1,
  input  [31:0] in_2,
  input  [31:0] in_3,
  input  [31:0] in_4,
  input  in_5,
  input  in_6,
  input  [5:0] tag,
  input  in_8,
  input  in_9,
  input  in_10,
  input  in_11,
  output [31:0] out_12,
  output [31:0] out_13,
  output [31:0] out_14,
  output [31:0] out_15,
  output out_16
);

  wire block1_out_14, block2_out_14, block3_out_14, block4_out_14, comparator_1_eq, comparator_2_eq,
       comparator_3_eq, comparator_4_eq, en, en1, en2, en3, en4, hit1, hit2, hit3, hit4, or_1_out;
  wire [5:0] block1_out_13, block2_out_13, block3_out_13, block4_out_13;
  wire [15:0] count1_out_7, count2_out_7, count3_out_7, count4_out_7;
  wire [31:0] multiplexer_1_out, multiplexer_2_out, multiplexer_3_out, multiplexer_4_out, multiplexer_5_out,
       multiplexer_6_out, multiplexer_7_out, multiplexer_8_out, out11, out12, out13, out14, out21, out22,
       out23, out24, out31, out32, out33, out34, out41, out42, out43, out44;

  cache_block block1 (
    .in_1(in_6), .in_3(in_5), .in_4(en1), .in_8(tag), .out_9(out11), .out_10(out12), .out_11(out13),
    .out_12(out14), .out_13(block1_out_13), .in_6(in_3), .in_7(in_4), .in_5(in_2), .in_2(in_1),
    .out_14(block1_out_14));
  cache_block block2 (
    .in_1(in_6), .in_3(in_5), .in_4(en2), .in_8(tag), .out_9(out21), .out_10(out22), .out_11(out23),
    .out_12(out24), .out_13(block2_out_13), .in_6(in_3), .in_7(in_4), .in_5(in_2), .in_2(in_1),
    .out_14(block2_out_14));
  cache_block block3 (
    .in_1(in_6), .in_3(in_5), .in_4(en3), .in_8(tag), .out_9(out31), .out_10(out32), .out_11(out33),
    .out_12(out34), .out_13(block3_out_13), .in_6(in_3), .in_7(in_4), .in_5(in_2), .in_2(in_1),
    .out_14(block3_out_14));
  and and_1 (en, in_11, ~in_10);  // AND_Gate
  cache_block block4 (
    .in_1(in_6), .in_3(in_5), .in_4(en4), .in_8(tag), .out_9(out41), .out_10(out42), .out_11(out43),
    .out_12(out44), .out_13(block4_out_13), .in_6(in_3), .in_7(in_4), .in_5(in_2), .in_2(in_1),
    .out_14(block4_out_14));
  Comparator #(.width(6)) comparator_1 (.a(block1_out_13), .b(tag), .eq(comparator_1_eq));  // open: gt, lt
  Comparator #(.width(6)) comparator_2 (.a(block2_out_13), .b(tag), .eq(comparator_2_eq));  // open: gt, lt
  Comparator #(.width(6)) comparator_3 (.a(block3_out_13), .b(tag), .eq(comparator_3_eq));  // open: gt, lt
  Comparator #(.width(6)) comparator_4 (.a(block4_out_13), .b(tag), .eq(comparator_4_eq));  // open: gt, lt
  and and_2 (hit1, comparator_1_eq, block1_out_14);
  and and_3 (hit2, comparator_2_eq, block2_out_14);
  and and_4 (hit3, comparator_3_eq, block3_out_14);
  and and_5 (hit4, comparator_4_eq, block4_out_14);
  counter count1 (.in_2(in_6), .in_3(en1), .in_4(hit1), .in_5(in_8), .out_7(count1_out_7), .in_1(in_5), .in_6(en));
  counter count2 (.in_2(in_6), .in_3(en2), .in_4(hit2), .in_5(in_8), .out_7(count2_out_7), .in_1(in_5), .in_6(en));
  counter count3 (.in_2(in_6), .in_3(en3), .in_4(hit3), .in_5(in_8), .out_7(count3_out_7), .in_1(in_5), .in_6(en));
  counter count4 (.in_2(in_6), .in_3(en4), .in_4(hit4), .in_5(in_8), .out_7(count4_out_7), .in_1(in_5), .in_6(en));
  Multiplexer #(.width(32)) multiplexer_1 (.in0(out11), .in1(out21), .out(multiplexer_1_out), .sel(hit2));  // open: en
  Multiplexer #(.width(32)) multiplexer_2 (.in0(out12), .in1(out22), .out(multiplexer_2_out), .sel(hit2));  // open: en
  Multiplexer #(.width(32)) multiplexer_3 (.in0(out13), .in1(out23), .out(multiplexer_3_out), .sel(hit2));  // open: en
  Multiplexer #(.width(32)) multiplexer_4 (.in0(out14), .in1(out24), .out(multiplexer_4_out), .sel(hit2));  // open: en
  Multiplexer #(.width(32)) multiplexer_5 (
    .in0(multiplexer_1_out), .in1(out31), .out(multiplexer_5_out), .sel(hit3));  // open: en
  Multiplexer #(.width(32)) multiplexer_6 (
    .in0(multiplexer_2_out), .in1(out32), .out(multiplexer_6_out), .sel(hit3));  // open: en
  Multiplexer #(.width(32)) multiplexer_7 (
    .in0(multiplexer_3_out), .in1(out33), .out(multiplexer_7_out), .sel(hit3));  // open: en
  Multiplexer #(.width(32)) multiplexer_8 (
    .in0(multiplexer_4_out), .in1(out34), .out(multiplexer_8_out), .sel(hit3));  // open: en
  or or_1 (or_1_out, hit1, hit2, hit3, hit4);
  Multiplexer #(.width(32)) multiplexer_9 (.in0(multiplexer_5_out), .in1(out41), .out(out_12), .sel(hit4));  // open: en
  Multiplexer #(.width(32)) multiplexer_10 (
    .in0(multiplexer_6_out), .in1(out42), .out(out_13), .sel(hit4));  // open: en
  Multiplexer #(.width(32)) multiplexer_11 (
    .in0(multiplexer_7_out), .in1(out43), .out(out_14), .sel(hit4));  // open: en
  Multiplexer #(.width(32)) multiplexer_12 (
    .in0(multiplexer_8_out), .in1(out44), .out(out_15), .sel(hit4));  // open: en
  LRU lru_1 (
    .in_1(count1_out_7), .in_2(count2_out_7), .in_3(count3_out_7), .in_4(count4_out_7), .in_5(hit1),
    .in_6(hit2), .in_7(hit3), .in_8(hit4), .in_9(in_8), .in_10(in_9), .in_11(en), .out_12(en1), .out_13(en2),
    .out_14(en3), .out_15(en4));
  and and_6 (out_16, in_11, or_1_out);

  // Other names for the same wires on the sheet: clk = in_5; groupen = in_11; in1[31:0] = in_1; in2[31:0] = in_2;
  //   in3[31:0] = in_3; in4[31:0] = in_4; MemRead = in_8; MemWrite = in_9; rst = in_6; stop = in_10
endmodule

module counter (
  input  in_1,
  input  in_2,
  input  in_3,
  input  in_4,
  input  in_5,
  input  in_6,
  output [15:0] out_7
);

  wire and_1_out, and_2_out, clr, count, or_1_out;

  and and_1 (and_1_out, in_4, in_5);
  and and_2 (and_2_out, ~in_4, in_5, in_3);  // AND_Gate
  Counter #(.width(16), .max('hffff)) counter_1 (
    .load(clr), .D({16{1'b0}}), .count(count), .Q(out_7), .clk(in_1), .clr(in_2));  // open: carry
  or or_1 (or_1_out, and_1_out, and_2_out);
  and and_3 (count, ~clr, in_6, in_5);  // AND_Gate
  and and_4 (clr, or_1_out, in_6);

  // Other names for the same wires on the sheet: BlockEnable = in_3; clk = in_1; en = in_6; Hit = in_4;
  //   MemRead = in_5; rst = in_2
endmodule

module LRU (
  input  [15:0] in_1,
  input  [15:0] in_2,
  input  [15:0] in_3,
  input  [15:0] in_4,
  input  in_5,
  input  in_6,
  input  in_7,
  input  in_8,
  input  in_9,
  input  in_10,
  input  in_11,
  output out_12,
  output out_13,
  output out_14,
  output out_15
);

  wire and_1_out, and_2_out, and_3_out, and_4_out, and_5_out, comparator_1_lt, comparator_2_lt,
       comparator_3_lt, demultiplexer_1_out0, demultiplexer_1_out1, demultiplexer_1_out2,
       demultiplexer_1_out3, or_1_out, or_2_out, or_3_out, or_4_out;
  wire [1:0] multiplexer_1_out, multiplexer_3_out, sel;
  wire [15:0] multiplexer_2_out, multiplexer_4_out;

  Comparator #(.width(16)) comparator_1 (.a(in_1), .b(in_2), .lt(comparator_1_lt));  // open: gt, eq
  Demultiplexer #(.select(2), .disabled(0)) demultiplexer_1 (
    .out0(demultiplexer_1_out0), .out1(demultiplexer_1_out1), .out2(demultiplexer_1_out2),
    .out3(demultiplexer_1_out3), .in(in_11), .sel(sel), .en(and_1_out));
  and and_1 (and_1_out, ~in_5, ~in_6, ~in_7, ~in_8, ~in_10);  // AND_Gate
  Multiplexer #(.width(2)) multiplexer_1 (
    .in0(2'b00), .in1(2'b01), .out(multiplexer_1_out), .sel(comparator_1_lt));  // open: en
  Multiplexer #(.width(16)) multiplexer_2 (
    .in0(in_1), .in1(in_2), .out(multiplexer_2_out), .sel(comparator_1_lt));  // open: en
  Comparator #(.width(16)) comparator_2 (.a(multiplexer_2_out), .b(in_3), .lt(comparator_2_lt));  // open: gt, eq
  Multiplexer #(.width(2)) multiplexer_3 (
    .in0(multiplexer_1_out), .in1(2'b10), .out(multiplexer_3_out), .sel(comparator_2_lt));  // open: en
  Multiplexer #(.width(16)) multiplexer_4 (
    .in0(multiplexer_2_out), .in1(in_3), .out(multiplexer_4_out), .sel(comparator_2_lt));  // open: en
  Comparator #(.width(16)) comparator_3 (.a(multiplexer_4_out), .b(in_4), .lt(comparator_3_lt));  // open: gt, eq
  and and_2 (and_2_out, in_5, in_10);
  and and_3 (and_3_out, in_6, in_10);
  and and_4 (and_4_out, in_7, in_10);
  and and_5 (and_5_out, in_8, in_10);
  Multiplexer #(.width(2)) multiplexer_5 (
    .in0(multiplexer_3_out), .in1(2'b11), .out(sel), .sel(comparator_3_lt));  // open: en
  Multiplexer multiplexer_6 (.in0(1'b0), .in1(in_11), .out(out_12), .sel(or_1_out));  // open: en
  or or_1 (or_1_out, and_2_out, demultiplexer_1_out0);
  Multiplexer multiplexer_7 (.in0(1'b0), .in1(in_11), .out(out_13), .sel(or_2_out));  // open: en
  or or_2 (or_2_out, and_3_out, demultiplexer_1_out1);
  Multiplexer multiplexer_8 (.in0(1'b0), .in1(in_11), .out(out_14), .sel(or_3_out));  // open: en
  or or_3 (or_3_out, and_4_out, demultiplexer_1_out2);
  Multiplexer multiplexer_9 (.in0(1'b0), .in1(in_11), .out(out_15), .sel(or_4_out));  // open: en
  or or_4 (or_4_out, and_5_out, demultiplexer_1_out3);

  // Other names for the same wires on the sheet: count1[15:0] = in_1; count2[15:0] = in_2; count3[15:0] = in_3;
  //   count4[15:0] = in_4; en = in_11; hit1 = in_5; hit2 = in_6; hit3 = in_7; hit4 = in_8; MemRead = in_9;
  //   MemWrite = in_10
endmodule

module cache_block (
  input  in_1,
  input  [31:0] in_2,
  input  in_3,
  input  in_4,
  input  [31:0] in_5,
  input  [31:0] in_6,
  input  [31:0] in_7,
  input  [5:0] in_8,
  output [31:0] out_9,
  output [31:0] out_10,
  output [31:0] out_11,
  output [31:0] out_12,
  output [5:0] out_13,
  output out_14
);

  Register #(.width(32)) register_1 (.D(in_2), .en(in_4), .Q(out_9), .clk(in_3), .clr(in_1));
  Register #(.width(32)) register_2 (.D(in_5), .en(in_4), .Q(out_10), .clk(in_3), .clr(in_1));
  Register #(.width(32)) register_3 (.D(in_6), .en(in_4), .Q(out_11), .clk(in_3), .clr(in_1));
  Register #(.width(32)) register_4 (.D(in_7), .en(in_4), .Q(out_12), .clk(in_3), .clr(in_1));
  Register #(.width(6)) register_5 (.D(in_8), .en(in_4), .Q(out_13), .clk(in_3), .clr(in_1));
  Register #(.width(1)) register_6 (.D(1'b1), .en(in_4), .Q(out_14), .clk(in_3), .clr(in_1));

  // Other names for the same wires on the sheet: clk = in_3; en = in_4; rst = in_1
endmodule

module ram (
  input  [1:0] MuxBlock,
  input  MemWrite,
  input  MemRead,
  input  Hit,
  input  [5:0] Tag,
  input  [1:0] MuxGroup,
  input  [31:0] MemData,
  input  Clk,
  input  Reset,
  output [31:0] _4,
  output [31:0] _3,
  output [31:0] _2,
  output out_13,
  output [31:0] _1
);

  wire _1_t, _2_t, _3_t, _4_t, and_1_out, and_2_out, counter_1_carry, not_1_out, not_2_out;
  wire [9:0] adder_1_out, adder_2_out, adder_3_out, adder_4_out, multiplexer_1_out;
  wire [31:0] ram_1_data, ram_2_data, ram_3_data, ram_4_data;

  and and_1 (and_1_out, MemRead, not_1_out);
  not not_1 (not_1_out, Hit);
  Counter #(.width(3), .max('h5)) counter_1 (
    .count(and_1_out), .carry(counter_1_carry), .clk(Clk), .clr(Reset));  // open: load, D, Q
  and and_2 (and_2_out, MemRead, Hit);
  and and_3 (out_13, and_1_out, not_2_out);
  not not_2 (not_2_out, counter_1_carry);
  Demultiplexer #(.select(2)) demultiplexer_1 (
    .out0(_1_t), .out1(_2_t), .out2(_3_t), .out3(_4_t), .in(MemWrite), .sel(MuxBlock));  // open: en
  Multiplexer #(.width(10), .enable("false")) multiplexer_1 (
    .in0({Tag, MuxGroup, 2'b00}), .in1({10{1'b0}}), .out(multiplexer_1_out), .sel(and_2_out));
  Adder #(.width(10)) adder_1 (.a(10'h3), .b(multiplexer_1_out), .out(adder_1_out));  // open: cin, cout
  Adder #(.width(10)) adder_2 (.a(10'h2), .b(multiplexer_1_out), .out(adder_2_out));  // open: cin, cout
  Adder #(.width(10)) adder_3 (.a(10'h1), .b(multiplexer_1_out), .out(adder_3_out));  // open: cin, cout
  Adder #(.width(10)) adder_4 (.a({10{1'b0}}), .b(multiplexer_1_out), .out(adder_4_out));  // open: cin, cout
  RAM #(.addrWidth(10), .dataWidth(32), .bus("separate")) ram_1 (
    .addr(adder_1_out), .din(MemData), .data(ram_1_data), .str(_4_t), .clk(Clk), .clr(Reset));  // open: sel, ld
  RAM #(.addrWidth(10), .dataWidth(32), .bus("separate")) ram_2 (
    .addr(adder_2_out), .din(MemData), .data(ram_2_data), .str(_3_t), .clk(Clk), .clr(Reset));  // open: sel, ld
  RAM #(.addrWidth(10), .dataWidth(32), .bus("separate")) ram_3 (
    .addr(adder_3_out), .din(MemData), .data(ram_3_data), .str(_2_t), .clk(Clk), .clr(Reset));  // open: sel, ld
  RAM #(.addrWidth(10), .dataWidth(32), .bus("separate")) ram_4 (
    .addr(adder_4_out), .din(MemData), .data(ram_4_data), .str(_1_t), .clk(Clk), .clr(Reset));  // open: sel, ld
  Multiplexer #(.width(32), .enable("false")) multiplexer_2 (.in0(ram_1_data), .in1(MemData), .out(_4), .sel(_4_t));
  Multiplexer #(.width(32), .enable("false")) multiplexer_3 (.in0(ram_2_data), .in1(MemData), .out(_3), .sel(_3_t));
  Multiplexer #(.width(32), .enable("false")) multiplexer_4 (.in0(ram_3_data), .in1(MemData), .out(_2), .sel(_2_t));
  Multiplexer #(.width(32), .enable("false")) multiplexer_5 (.in0(ram_4_data), .in1(MemData), .out(_1), .sel(_1_t));

  // Other names for the same wires on the sheet: Data[31:0] = MemData
endmodule
